// Logisim project Parte2-Trabalho.circ as structural Verilog: 9 circuits, main circuit main
module main (
  output [4:0] out_1,
  output [4:0] out_2,
  output [4:0] out_3,
  output [31:0] out_4,
  output [31:0] out_5,
  output [31:0] out_6,
  output [2:0] out_7
);

  wire ALUSrc, and_1_out, Branch, CLK, Jump, MemToReg, MemWrite, RegDest, RegDst, RegWrite, Reset,
       ResetRegFile, ula_1_zero;
  wire [1:0] controlunit_1_aluop;
  wire [5:0] Funct, OPCODE;
  wire [15:6] instructionmemory_1_rd;
  wire [27:0] adder_1_out, bit_extender_1_out;
  wire [31:0] adder_2_out, bit_extender_2_out, datamemory_1_rd, multiplexer_1_out, multiplexer_2_out,
       multiplexer_4_out, register_1_q, registerfile_1_readdata1, registerfile_1_readdata2, shifter_1_out,
       shifter_2_out;

  Multiplexer #(.width(32)) multiplexer_1 (
    .in0({shifter_1_out[31:28], adder_1_out}), .in1(adder_2_out), .out(multiplexer_1_out), .sel(and_1_out));
  Multiplexer #(.width(32)) multiplexer_2 (
    .in0(multiplexer_1_out), .in1(shifter_1_out), .out(multiplexer_2_out), .sel(Jump));
  Register #(.width(32)) register_1 (.D(multiplexer_2_out), .en(1'b1), .clk(CLK), .Q(register_1_q), .clr(Reset));
  Button button_1 (.out(ResetRegFile));
  Adder #(.width(32)) adder_1 (
    .a(register_1_q), .b(32'h4), .out({shifter_1_out[31:28], adder_1_out}), .cin(1'b0));  // open: cout
  Clock clock_1 (.out(CLK));
  InstructionMemory instructionmemory_1 (.A(register_1_q), .RD({OPCODE, out_1, out_2, instructionmemory_1_rd, Funct}));
  Button button_2 (.out(Reset));
  assign bit_extender_1_out = {{2{out_1[4]}}, {out_1, out_2, instructionmemory_1_rd, Funct}};  // Bit_Extender bit_extender_1
  LED led_1 (.in(MemToReg));
  LED led_2 (.in(MemWrite));
  LED led_3 (.in(Branch));
  LED led_4 (.in(ALUSrc));
  LED led_5 (.in(RegDest));
  LED led_6 (.in(RegWrite));
  LED led_7 (.in(Jump));
  Shifter #(.width(28)) shifter_1 (.in(bit_extender_1_out), .\dist (5'b00010), .out(shifter_1_out[27:0]));
  RegisterFile registerfile_1 (
    .CLK(CLK), .Reset(ResetRegFile), .ReadReg1(out_1), .WriteReg(out_3), .WD3(out_4), .WriteEnable(RegWrite),
    .ReadReg2(out_2), .ReadData1(registerfile_1_readdata1), .ReadData2(registerfile_1_readdata2));
  assign bit_extender_2_out = {{16{instructionmemory_1_rd[15]}}, {instructionmemory_1_rd, Funct}};  // Bit_Extender bit_extender_2
  Multiplexer #(.width(5)) multiplexer_3 (.in0(out_2), .in1(instructionmemory_1_rd[15:11]), .out(out_3), .sel(RegDst));
  ControlUnit controlunit_1 (
    .Opcode(OPCODE), .ALUOp(controlunit_1_aluop), .Jump(Jump), .RegDst(RegDst), .Branch(Branch),
    .MemWrite(MemWrite), .MemToReg(MemToReg), .ALUSrc(ALUSrc), .RegWrite(RegWrite));
  ULADECODER uladecoder_1 (.ALUOp(controlunit_1_aluop), .Funct(Funct), .ALUControl(out_7));
  Multiplexer #(.width(32)) multiplexer_4 (
    .in0(registerfile_1_readdata2), .in1(bit_extender_2_out), .out(multiplexer_4_out), .sel(ALUSrc));
  Shifter #(.width(32)) shifter_2 (.in(bit_extender_2_out), .\dist (5'b00010), .out(shifter_2_out));
  ULA ula_1 (
    .A(registerfile_1_readdata1), .B(multiplexer_4_out), .Alucontrol(out_7), .ALUResult(out_6),
    .Zero(ula_1_zero));
  Adder #(.width(32)) adder_2 (
    .a(shifter_2_out), .b({shifter_1_out[31:28], adder_1_out}), .out(adder_2_out));  // open: cin, cout
  and and_1 (and_1_out, Branch, ula_1_zero);
  DataMemory datamemory_1 (.CLOCK(CLK), .A(out_6), .WD(registerfile_1_readdata2), .WE(MemWrite), .RD(datamemory_1_rd));
  Multiplexer #(.width(32)) multiplexer_5 (.in0(datamemory_1_rd), .out(out_5), .sel(MemToReg));  // open: in1
  Multiplexer #(.width(32)) multiplexer_6 (.in0(out_6), .in1(datamemory_1_rd), .out(out_4), .sel(MemToReg));

  // Other names for the same wires on the sheet: rt[4:0] = out_2; rs[4:0] = out_1; ALUCONTROL[2:0] = out_7;
  //   ALUResult[31:0] = out_6; MemRead[31:0] = out_5; Registrado_Destino[4:0] = out_3; WriteData[31:0] = out_4

  // Notes on the sheet:
  //   PCSrc
  //   ReadData
endmodule

module ULA (
  input  [31:0] A,
  input  [31:0] B,
  input  [2:0] Alucontrol,
  output Zero,
  output [31:0] ALUResult
);

  wire adder_1_cout, msb_1_out_2;
  wire [31:0] adder_1_out, and_1_out, extensor_1_out_2, multiplexer_1_out, not_1_out, or_1_out;

  assign not_1_out = ~B;  // NOT_Gate not_1, 32 bits wide
  Multiplexer #(.width(32)) multiplexer_1 (.in0(B), .in1(not_1_out), .out(multiplexer_1_out), .sel(Alucontrol[2]));
  Adder #(.width(32)) adder_1 (
    .a(A), .b(multiplexer_1_out), .out(adder_1_out), .cin(Alucontrol[2]), .cout(adder_1_cout));
  // Probe on adder_1_cout
  assign and_1_out = A & multiplexer_1_out;  // AND_Gate and_1, 32 bits wide
  assign or_1_out = A | multiplexer_1_out;  // OR_Gate or_1, 32 bits wide
  MSB msb_1 (.in_1(adder_1_out), .out_2(msb_1_out_2));
  Extensor extensor_1 (.in_1(msb_1_out_2), .out_2(extensor_1_out_2));
  Multiplexer #(.select(2), .width(32)) multiplexer_2 (
    .in0(and_1_out), .in1(or_1_out), .in2(adder_1_out), .in3(extensor_1_out_2), .out(ALUResult),
    .sel(Alucontrol[1:0]));
  Comparator #(.width(32)) comparator_1 (.a({32{1'b0}}), .b(ALUResult), .eq(Zero));  // open: gt, lt
endmodule

module Extensor (
  input  in_1,
  output [31:0] out_2
);


  assign out_2 = {{31{1'b0}}, in_1};
endmodule

module MSB (
  input  [31:0] in_1,
  output out_2
);


  assign out_2 = in_1[31];
endmodule

module RegisterFile (
  input  CLK,
  input  [4:0] ReadReg1,
  input  [4:0] ReadReg2,
  input  [31:0] WD3,
  input  [4:0] WriteReg,
  input  WriteEnable,
  input  Reset,
  output [31:0] ReadData1,
  output [31:0] ReadData2
);

  wire s0, s1, s2, s3, s4, s5, s6, s7, s8, s9, s10, s11, s12, s13, s14, s15, s16, s17, s18, s19, s20, s21,
       s22, s23, s24, s25, s26, s27, s28, s29, s30, s31;
  wire [31:0] d0, d1, d2, d3, d4, d5, d6, d7, d8, d9, d10, d11, d12, d13, d14, d15, d16, d17, d18, d19, d20,
       d21, d22, d23, d24, d25, d26, d27, d28, d29, d30, d31;

  Register #(.width(32)) register_1 (.D(WD3), .en(s0), .clk(CLK), .Q(d0), .clr(Reset));
  Register #(.width(32)) register_2 (.D(WD3), .en(s1), .clk(CLK), .Q(d1), .clr(Reset));
  Register #(.width(32)) register_3 (.D(WD3), .en(s2), .clk(CLK), .Q(d2), .clr(Reset));
  Register #(.width(32)) register_4 (.D(WD3), .en(s3), .clk(CLK), .Q(d3), .clr(Reset));
  Register #(.width(32)) register_5 (.D(WD3), .en(s4), .clk(CLK), .Q(d4), .clr(Reset));
  Register #(.width(32)) register_6 (.D(WD3), .en(s5), .clk(CLK), .Q(d5), .clr(Reset));
  Register #(.width(32)) register_7 (.D(WD3), .en(s6), .clk(CLK), .Q(d6), .clr(Reset));
  Register #(.width(32)) register_8 (.D(WD3), .en(s7), .clk(CLK), .Q(d7), .clr(Reset));
  Register #(.width(32)) register_9 (.D(WD3), .en(s16), .clk(CLK), .Q(d16), .clr(Reset));
  Register #(.width(32)) register_10 (.D(WD3), .en(s17), .clk(CLK), .Q(d17), .clr(Reset));
  Register #(.width(32)) register_11 (.D(WD3), .en(s18), .clk(CLK), .Q(d18), .clr(Reset));
  Register #(.width(32)) register_12 (.D(WD3), .en(s19), .clk(CLK), .Q(d19), .clr(Reset));
  Register #(.width(32)) register_13 (.D(WD3), .en(s20), .clk(CLK), .Q(d20), .clr(Reset));
  Register #(.width(32)) register_14 (.D(WD3), .en(s21), .clk(CLK), .Q(d21), .clr(Reset));
  Register #(.width(32)) register_15 (.D(WD3), .en(s22), .clk(CLK), .Q(d22), .clr(Reset));
  Register #(.width(32)) register_16 (.D(WD3), .en(s23), .clk(CLK), .Q(d23), .clr(Reset));
  Register #(.width(32)) register_17 (.D(WD3), .en(s8), .clk(CLK), .Q(d8), .clr(Reset));
  Register #(.width(32)) register_18 (.D(WD3), .en(s9), .clk(CLK), .Q(d9), .clr(Reset));
  Register #(.width(32)) register_19 (.D(WD3), .en(s10), .clk(CLK), .clr(Reset));  // open: Q
  Register #(.width(32)) register_20 (.D(WD3), .en(s11), .clk(CLK), .Q(d11), .clr(Reset));
  Register #(.width(32)) register_21 (.en(s12), .clk(CLK), .Q(d12), .clr(Reset));  // open: D
  Register #(.width(32)) register_22 (.en(s13), .clk(CLK), .Q(d13), .clr(Reset));  // open: D
  Register #(.width(32)) register_23 (.D(WD3), .en(s14), .clk(CLK), .Q(d14), .clr(Reset));
  Register #(.width(32)) register_24 (.D(WD3), .en(s15), .clk(CLK), .Q(d15), .clr(Reset));
  Register #(.width(32)) register_25 (.D(WD3), .en(s24), .clk(CLK), .Q(d24), .clr(Reset));
  Register #(.width(32)) register_26 (.D(WD3), .en(s25), .clk(CLK), .Q(d25), .clr(Reset));
  Register #(.width(32)) register_27 (.D(WD3), .en(s26), .clk(CLK), .Q(d26), .clr(Reset));
  Register #(.width(32)) register_28 (.D(WD3), .en(s27), .clk(CLK), .Q(d27), .clr(Reset));
  Register #(.width(32)) register_29 (.D(WD3), .en(s28), .clk(CLK), .Q(d28), .clr(Reset));
  Register #(.width(32)) register_30 (.en(s29), .clk(CLK), .Q(d29), .clr(Reset));  // open: D
  Register #(.width(32)) register_31 (.D(WD3), .en(s30), .clk(CLK), .Q(d30), .clr(Reset));
  Register #(.width(32)) register_32 (.D(WD3), .en(s31), .clk(CLK), .Q(d31), .clr(Reset));
  Multiplexer #(.select(5), .width(32)) multiplexer_1 (
    .in0(d0), .in1(d1), .in2(d2), .in3(d3), .in4(d4), .in5(d5), .in6(d6), .in7(d7), .in8(d8), .in9(d9),
    .in10(d10), .in11(d11), .in12(d12), .in13(d13), .in14(d14), .in15(d15), .in16(d16), .in17(d17),
    .in18(d18), .in19(d19), .in20(d20), .in21(d21), .in22(d22), .in23(d23), .in24(d24), .in25(d25),
    .in26(d26), .in27(d27), .in28(d28), .in29(d29), .in30(d30), .in31(d31), .out(ReadData1), .sel(ReadReg1));
  Demultiplexer #(.select(5)) demultiplexer_1 (
    .out0(s0), .out1(s1), .out2(s2), .out3(s3), .out4(s4), .out5(s5), .out6(s6), .out7(s7), .out8(s8),
    .out9(s9), .out10(s10), .out11(s11), .out12(s12), .out13(s13), .out14(s14), .out15(s15), .out16(s16),
    .out17(s17), .out18(s18), .out19(s19), .out20(s20), .out21(s21), .out22(s22), .out23(s23), .out24(s24),
    .out25(s25), .out26(s26), .out27(s27), .out28(s28), .out29(s29), .out30(s30), .out31(s31),
    .in(WriteEnable), .sel(WriteReg));
  Multiplexer #(.enable("true"), .select(5), .width(32)) multiplexer_2 (
    .in0(d0), .in1(d1), .in2(d2), .in3(d3), .in4(d4), .in5(d5), .in6(d6), .in7(d7), .in8(d8), .in9(d9),
    .in10(d10), .in11(d11), .in12(d12), .in13(d13), .in14(d14), .in15(d15), .in16(d16), .in17(d17),
    .in18(d18), .in19(d19), .in20(d20), .in21(d21), .in22(d22), .in23(d23), .in24(d24), .in25(d25),
    .in26(d26), .in27(d27), .in28(d28), .in29(d29), .in30(d30), .in31(d31), .out(ReadData2), .sel(ReadReg2));  // open: en

  // Other names for the same wires on the sheet: Data[31:0] = WD3
endmodule

module InstructionMemory (
  input  [31:0] A,
  output [31:0] RD
);

  ROM #(.addrWidth(9), .dataWidth(32)) rom_1 (.addr(A[10:2]), .data(RD));

  // Notes on the sheet:
  //   contents of rom_1 (hex, n*v repeats v):
  //   20020005 2003000c 2067fff7 e22025 642824 a42820 10a70008 64202a 10800001 2005000a e2202a 853820
  //   e23822 ac670044 8c020050 8000011 20020001 ac020054
endmodule

module DataMemory (
  input  [31:0] A,
  input  WE,
  input  CLOCK,
  input  [31:0] WD,
  output [31:0] RD
);

  RAM #(.addrWidth(10), .dataWidth(32), .enables("line"), .\type ("nonvolatile")) ram_1 (
    .addr(A[11:2]), .we(WE), .clk(CLOCK), .din(WD), .dout(RD));
endmodule

module ControlUnit (
  input  [5:0] Opcode,
  output Jump,
  output RegDst,
  output Branch,
  output MemWrite,
  output MemToReg,
  output RegWrite,
  output ALUSrc,
  output [1:0] ALUOp
);

  wire ADDI_out;

  and Tipo_R (ALUOp[1], ~Opcode[5], ~Opcode[4], ~Opcode[3], ~Opcode[2], ~Opcode[1], ~Opcode[0]);  // AND_Gate
  and LW (MemToReg, Opcode[5], ~Opcode[4], ~Opcode[3], ~Opcode[2], Opcode[1], Opcode[0]);  // AND_Gate
  and SW (MemWrite, Opcode[5], ~Opcode[4], Opcode[3], ~Opcode[2], Opcode[1], Opcode[0]);  // AND_Gate
  and BEQ (ALUOp[0], ~Opcode[5], ~Opcode[4], ~Opcode[3], Opcode[2], ~Opcode[1], ~Opcode[0]);  // AND_Gate
  and ADDI (ADDI_out, ~Opcode[5], ~Opcode[4], Opcode[3], ~Opcode[2], ~Opcode[1], ~Opcode[0]);  // AND_Gate
  and J (Jump, ~Opcode[5], ~Opcode[4], ~Opcode[3], ~Opcode[2], Opcode[1], ~Opcode[0]);  // AND_Gate
  or or_1 (RegWrite, ADDI_out, MemToReg, ALUOp[1]);
  nor nor_1 (ALUSrc, ALUOp[0], ALUOp[1]);

  assign Branch = ALUOp[0];
  assign RegDst = ALUOp[1];
endmodule

module ULADECODER (
  input  [5:0] Funct,
  input  [1:0] ALUOp,
  output [2:0] ALUControl
);

  wire ADD_out, AND_out, priority_encoder_1_p2, SUB_out;
  wire [2:0] priority_encoder_1_p4;

  and ADD (ADD_out, ~Funct[3], ~Funct[2], ~Funct[1], ~Funct[0]);  // AND_Gate
  and SUB (SUB_out, ~Funct[3], ~Funct[2], Funct[1], ~Funct[0]);  // AND_Gate
  and AND (AND_out, ~Funct[3], Funct[2], ~Funct[1], ~Funct[0]);  // AND_Gate
  // Priority_Encoder priority_encoder_1: pin names not known; wires that end beside it: AND_out, priority_encoder_1_p2, ADD_out, priority_encoder_1_p4, SUB_out, priority_encoder_1_p2
  Multiplexer #(.select(2), .width(3)) multiplexer_1 (
    .in0(3'b010), .in1(3'b110), .in2(priority_encoder_1_p4), .in3(priority_encoder_1_p4), .out(ALUControl),
    .sel(ALUOp));
  and OR (priority_encoder_1_p2, ~Funct[3], Funct[2], ~Funct[1], Funct[0]);  // AND_Gate
  and SLT (priority_encoder_1_p2, Funct[3], ~Funct[2], Funct[1], ~Funct[0]);  // AND_Gate

  // Notes on the sheet:
  //   SUB
  //   ADD
endmodule
