// Logisim project Trab-2.circ as structural Verilog: 9 circuits, main circuit main
module main (
  output [31:0] out_1,
  output [4:0] out_2,
  output [4:0] out_3,
  output [4:0] out_4,
  output [31:0] out_5
);

  wire alu_1_zero, and_1_out, CLK, maindecoder_1_alusrc, maindecoder_1_branch, maindecoder_1_jump,
       maindecoder_1_memtoreg, maindecoder_1_memwrite, maindecoder_1_regdest, maindecoder_1_regwrite, Reset;
  wire [1:0] maindecoder_1_aluop;
  wire [2:0] aludecoder_1_alucontrol;
  wire [27:0] adder_1_out, bit_extender_1_out;
  wire [31:0] adder_2_out, alu_1_aluresult, bit_extender_2_out, datamemory_1_rd, multiplexer_1_out,
       multiplexer_2_out, multiplexer_4_out, multiplexer_5_out, register_1_q, registerfile_1_rd1,
       registerfile_1_rd2, shifter_1_out, shifter_2_out;

  Multiplexer #(.width(32)) multiplexer_1 (
    .in0({shifter_1_out[31:28], adder_1_out}), .in1(adder_2_out), .out(multiplexer_1_out), .sel(and_1_out));
  Multiplexer #(.width(32)) multiplexer_2 (
    .in0(multiplexer_1_out), .in1(shifter_1_out), .out(multiplexer_2_out), .sel(maindecoder_1_jump));
  Clock clock_1 (.out(CLK));
  Register #(.width(32)) register_1 (.D(multiplexer_2_out), .en(1'b1), .clk(CLK), .Q(register_1_q), .clr(Reset));
  Button button_1 (.out(Reset));
  Adder #(.width(32)) adder_1 (
    .a(register_1_q), .b(32'h4), .out({shifter_1_out[31:28], adder_1_out}), .cin(1'b0));  // open: cout
  InstructionMemory instructionmemory_1 (.A(register_1_q), .RD(out_1));
  assign bit_extender_1_out = {{2{out_1[25]}}, out_1[25:0]};  // Bit_Extender bit_extender_1
  Shifter #(.width(28)) shifter_1 (.in(bit_extender_1_out), .\dist (5'b00010), .out(shifter_1_out[27:0]));
  MainDecoder maindecoder_1 (
    .Opcode(out_1[31:26]), .Jump(maindecoder_1_jump), .RegDest(maindecoder_1_regdest),
    .Branch(maindecoder_1_branch), .MemWrite(maindecoder_1_memwrite), .MemToReg(maindecoder_1_memtoreg),
    .RegWrite(maindecoder_1_regwrite), .ALUSrc(maindecoder_1_alusrc), .ALUOp(maindecoder_1_aluop));
  ALUDecoder aludecoder_1 (.ALUOp(maindecoder_1_aluop), .Funct(out_1[5:0]), .ALUControl(aludecoder_1_alucontrol));
  RegisterFile registerfile_1 (
    .CLK(CLK), .A2(out_1[20:16]), .A1(out_1[25:21]), .A3(out_4), .WE3(maindecoder_1_regwrite),
    .WD3(multiplexer_5_out), .RD1(registerfile_1_rd1), .RD2(registerfile_1_rd2));
  assign bit_extender_2_out = {{16{out_1[15]}}, out_1[15:0]};  // Bit_Extender bit_extender_2
  Multiplexer #(.width(5)) multiplexer_3 (
    .in0(out_1[20:16]), .in1(out_1[15:11]), .out(out_4), .sel(maindecoder_1_regdest));
  Multiplexer #(.width(32)) multiplexer_4 (
    .in0(registerfile_1_rd2), .in1(bit_extender_2_out), .out(multiplexer_4_out), .sel(maindecoder_1_alusrc));
  ALU alu_1 (
    .A(registerfile_1_rd1), .B(multiplexer_4_out), .Alucontrol(aludecoder_1_alucontrol),
    .ALUResult(alu_1_aluresult), .Zero(alu_1_zero));
  Shifter #(.width(32)) shifter_2 (.in(bit_extender_2_out), .\dist (5'b00010), .out(shifter_2_out));
  Adder #(.width(32)) adder_2 (
    .a(shifter_2_out), .b({shifter_1_out[31:28], adder_1_out}), .out(adder_2_out));  // open: cin, cout
  and and_1 (and_1_out, maindecoder_1_branch, alu_1_zero);
  DataMemory datamemory_1 (
    .CLOCK(CLK), .A(alu_1_aluresult), .WD(registerfile_1_rd2), .WE(maindecoder_1_memwrite),
    .RD(datamemory_1_rd));
  Multiplexer #(.width(32)) multiplexer_5 (
    .in0(alu_1_aluresult), .in1(datamemory_1_rd), .out(multiplexer_5_out), .sel(maindecoder_1_memtoreg));
  Multiplexer #(.width(32)) multiplexer_6 (
    .in1(datamemory_1_rd), .out(out_5), .sel(maindecoder_1_memtoreg));  // open: in0

  assign out_2 = out_1[25:21];
  assign out_3 = out_1[20:16];

  // Other names for the same wires on the sheet: A3[4:0] = out_4; Instruction[31:0] = out_1; A2[4:0] = out_1[20:16];
  //   A1[4:0] = out_1[25:21]; Read[31:0] = out_5

  // Notes on the sheet:
  //   PC + 4
  //   Alunos:
  //   rt
  //   Control Unit
  //   rs
  //   rt/rd
  //   Vinícius Mariano de Campos
  //   Danilo Barbosa da Silva
  //   SignImm
  //   PCBranch
  //   PCSrc
  //   ReadData
endmodule

module ALU (
  input  [31:0] A,
  input  [31:0] B,
  input  [2:0] Alucontrol,
  output Zero,
  output [31:0] ALUResult
);

  wire adder_1_cout, bitmaissignificativo_1_out_2;
  wire [31:0] adder_1_out, and_1_out, multiplexer_1_out, not_1_out, or_1_out, zeroextend_1_out_2;

  assign not_1_out = ~B;  // NOT_Gate not_1, 32 bits wide
  Multiplexer #(.width(32)) multiplexer_1 (.in0(B), .in1(not_1_out), .out(multiplexer_1_out), .sel(Alucontrol[2]));
  Adder #(.width(32)) adder_1 (
    .a(A), .b(multiplexer_1_out), .out(adder_1_out), .cin(Alucontrol[2]), .cout(adder_1_cout));
  // Probe on adder_1_cout
  assign and_1_out = A & multiplexer_1_out;  // AND_Gate and_1, 32 bits wide
  assign or_1_out = A | multiplexer_1_out;  // OR_Gate or_1, 32 bits wide
  Bitmaissignificativo bitmaissignificativo_1 (.in_1(adder_1_out), .out_2(bitmaissignificativo_1_out_2));
  zeroExtend zeroextend_1 (.in_1(bitmaissignificativo_1_out_2), .out_2(zeroextend_1_out_2));
  Multiplexer #(.select(2), .width(32)) multiplexer_2 (
    .in0(and_1_out), .in1(or_1_out), .in2(adder_1_out), .in3(zeroextend_1_out_2), .out(ALUResult),
    .sel(Alucontrol[1:0]));
  Comparator #(.width(32)) comparator_1 (.a({32{1'b0}}), .b(ALUResult), .eq(Zero));  // open: gt, lt
endmodule

module zeroExtend (
  input  in_1,
  output [31:0] out_2
);


  assign out_2 = {{31{1'b0}}, in_1};
endmodule

module Bitmaissignificativo (
  input  [31:0] in_1,
  output out_2
);


  assign out_2 = in_1[31];
endmodule

module RegisterFile (
  input  CLK,
  input  [4:0] A1,
  input  WE3,
  input  [4:0] A3,
  input  [31:0] WD3,
  input  [4:0] A2,
  output [31:0] RD1,
  output [31:0] RD2
);

  wire demultiplexer_1_out0, demultiplexer_1_out1, demultiplexer_1_out2, demultiplexer_1_out3,
       demultiplexer_1_out4, demultiplexer_1_out5, demultiplexer_1_out6, demultiplexer_1_out7,
       demultiplexer_1_out8, demultiplexer_1_out9, demultiplexer_1_out10, demultiplexer_1_out11,
       demultiplexer_1_out12, demultiplexer_1_out13, demultiplexer_1_out14, demultiplexer_1_out15,
       demultiplexer_1_out16, demultiplexer_1_out17, demultiplexer_1_out18, demultiplexer_1_out19,
       demultiplexer_1_out20, demultiplexer_1_out21, demultiplexer_1_out22, demultiplexer_1_out23,
       demultiplexer_1_out24, demultiplexer_1_out25, demultiplexer_1_out26, demultiplexer_1_out27,
       demultiplexer_1_out28, demultiplexer_1_out29, demultiplexer_1_out30, demultiplexer_1_out31;
  wire [31:0] register_1_q, register_2_q, register_3_q, register_4_q, register_5_q, register_6_q,
       register_7_q, register_8_q, register_9_q, register_10_q, register_11_q, register_12_q, register_13_q,
       register_14_q, register_15_q, register_16_q, register_17_q, register_18_q, register_19_q,
       register_20_q, register_21_q, register_22_q, register_23_q, register_24_q, register_25_q,
       register_26_q, register_27_q, register_28_q, register_29_q, register_30_q, register_31_q,
       register_32_q;

  Demultiplexer #(.select(5)) demultiplexer_1 (
    .out0(demultiplexer_1_out0), .out1(demultiplexer_1_out1), .out2(demultiplexer_1_out2),
    .out3(demultiplexer_1_out3), .out4(demultiplexer_1_out4), .out5(demultiplexer_1_out5),
    .out6(demultiplexer_1_out6), .out7(demultiplexer_1_out7), .out8(demultiplexer_1_out8),
    .out9(demultiplexer_1_out9), .out10(demultiplexer_1_out10), .out11(demultiplexer_1_out11),
    .out12(demultiplexer_1_out12), .out13(demultiplexer_1_out13), .out14(demultiplexer_1_out14),
    .out15(demultiplexer_1_out15), .out16(demultiplexer_1_out16), .out17(demultiplexer_1_out17),
    .out18(demultiplexer_1_out18), .out19(demultiplexer_1_out19), .out20(demultiplexer_1_out20),
    .out21(demultiplexer_1_out21), .out22(demultiplexer_1_out22), .out23(demultiplexer_1_out23),
    .out24(demultiplexer_1_out24), .out25(demultiplexer_1_out25), .out26(demultiplexer_1_out26),
    .out27(demultiplexer_1_out27), .out28(demultiplexer_1_out28), .out29(demultiplexer_1_out29),
    .out30(demultiplexer_1_out30), .out31(demultiplexer_1_out31), .in(WE3), .sel(A3));
  Register #(.width(32)) register_1 (.D(WD3), .en(demultiplexer_1_out0), .clk(CLK), .Q(register_1_q));  // open: clr
  Register #(.width(32)) register_2 (.D(WD3), .en(demultiplexer_1_out1), .clk(CLK), .Q(register_2_q));  // open: clr
  Register #(.width(32)) register_3 (.D(WD3), .en(demultiplexer_1_out2), .clk(CLK), .Q(register_3_q));  // open: clr
  Register #(.width(32)) register_4 (.D(WD3), .en(demultiplexer_1_out3), .clk(CLK), .Q(register_4_q));  // open: clr
  Register #(.width(32)) register_5 (.D(WD3), .en(demultiplexer_1_out4), .clk(CLK), .Q(register_5_q));  // open: clr
  Register #(.width(32)) register_6 (.D(WD3), .en(demultiplexer_1_out5), .clk(CLK), .Q(register_6_q));  // open: clr
  Register #(.width(32)) register_7 (.D(WD3), .en(demultiplexer_1_out6), .clk(CLK), .Q(register_7_q));  // open: clr
  Register #(.width(32)) register_8 (.D(WD3), .en(demultiplexer_1_out7), .clk(CLK), .Q(register_8_q));  // open: clr
  Register #(.width(32)) register_9 (.D(WD3), .en(demultiplexer_1_out8), .clk(CLK), .Q(register_9_q));  // open: clr
  Register #(.width(32)) register_10 (.D(WD3), .en(demultiplexer_1_out9), .clk(CLK), .Q(register_10_q));  // open: clr
  Register #(.width(32)) register_11 (.D(WD3), .en(demultiplexer_1_out10), .clk(CLK), .Q(register_11_q));  // open: clr
  Register #(.width(32)) register_12 (.D(WD3), .en(demultiplexer_1_out11), .clk(CLK), .Q(register_12_q));  // open: clr
  Register #(.width(32)) register_13 (.D(WD3), .en(demultiplexer_1_out12), .clk(CLK), .Q(register_13_q));  // open: clr
  Register #(.width(32)) register_14 (.D(WD3), .en(demultiplexer_1_out13), .clk(CLK), .Q(register_14_q));  // open: clr
  Register #(.width(32)) register_15 (.D(WD3), .en(demultiplexer_1_out14), .clk(CLK), .Q(register_15_q));  // open: clr
  Register #(.width(32)) register_16 (.D(WD3), .en(demultiplexer_1_out15), .clk(CLK), .Q(register_16_q));  // open: clr
  Register #(.width(32)) register_17 (.D(WD3), .en(demultiplexer_1_out16), .clk(CLK), .Q(register_17_q));  // open: clr
  Register #(.width(32)) register_18 (.D(WD3), .en(demultiplexer_1_out17), .clk(CLK), .Q(register_18_q));  // open: clr
  Register #(.width(32)) register_19 (.D(WD3), .en(demultiplexer_1_out18), .clk(CLK), .Q(register_19_q));  // open: clr
  Register #(.width(32)) register_20 (.D(WD3), .en(demultiplexer_1_out19), .clk(CLK), .Q(register_20_q));  // open: clr
  Register #(.width(32)) register_21 (.D(WD3), .en(demultiplexer_1_out20), .clk(CLK), .Q(register_21_q));  // open: clr
  Register #(.width(32)) register_22 (.D(WD3), .en(demultiplexer_1_out21), .clk(CLK), .Q(register_22_q));  // open: clr
  Register #(.width(32)) register_23 (.D(WD3), .en(demultiplexer_1_out22), .clk(CLK), .Q(register_23_q));  // open: clr
  Register #(.width(32)) register_24 (.D(WD3), .en(demultiplexer_1_out23), .clk(CLK), .Q(register_24_q));  // open: clr
  Register #(.width(32)) register_25 (.D(WD3), .en(demultiplexer_1_out24), .clk(CLK), .Q(register_25_q));  // open: clr
  Register #(.width(32)) register_26 (.D(WD3), .en(demultiplexer_1_out25), .clk(CLK), .Q(register_26_q));  // open: clr
  Register #(.width(32)) register_27 (.D(WD3), .en(demultiplexer_1_out26), .clk(CLK), .Q(register_27_q));  // open: clr
  Register #(.width(32)) register_28 (.D(WD3), .en(demultiplexer_1_out27), .clk(CLK), .Q(register_28_q));  // open: clr
  Register #(.width(32)) register_29 (.D(WD3), .en(demultiplexer_1_out28), .clk(CLK), .Q(register_29_q));  // open: clr
  Register #(.width(32)) register_30 (.D(WD3), .en(demultiplexer_1_out29), .clk(CLK), .Q(register_30_q));  // open: clr
  Register #(.width(32)) register_31 (.D(WD3), .en(demultiplexer_1_out30), .clk(CLK), .Q(register_31_q));  // open: clr
  Register #(.width(32)) register_32 (.D(WD3), .en(demultiplexer_1_out31), .clk(CLK), .Q(register_32_q));  // open: clr
  Multiplexer #(.select(5), .width(32)) multiplexer_1 (
    .in0(register_1_q), .in1(register_2_q), .in2(register_3_q), .in3(register_4_q), .in4(register_5_q),
    .in5(register_6_q), .in6(register_7_q), .in7(register_8_q), .in8(register_9_q), .in9(register_10_q),
    .in10(register_11_q), .in11(register_12_q), .in12(register_13_q), .in13(register_14_q),
    .in14(register_15_q), .in15(register_16_q), .in16(register_17_q), .in17(register_18_q),
    .in18(register_19_q), .in19(register_20_q), .in20(register_21_q), .in21(register_22_q),
    .in22(register_23_q), .in23(register_24_q), .in24(register_25_q), .in25(register_26_q),
    .in26(register_27_q), .in27(register_28_q), .in28(register_29_q), .in29(register_30_q),
    .in30(register_31_q), .in31(register_32_q), .out(RD1), .sel(A1));
  Multiplexer #(.select(5), .width(32)) multiplexer_2 (
    .in0(register_1_q), .in1(register_2_q), .in2(register_3_q), .in3(register_4_q), .in4(register_5_q),
    .in5(register_6_q), .in6(register_7_q), .in7(register_8_q), .in8(register_9_q), .in9(register_10_q),
    .in10(register_11_q), .in11(register_12_q), .in12(register_13_q), .in13(register_14_q),
    .in14(register_15_q), .in15(register_16_q), .in16(register_17_q), .in17(register_18_q),
    .in18(register_19_q), .in19(register_20_q), .in20(register_21_q), .in21(register_22_q),
    .in22(register_23_q), .in23(register_24_q), .in24(register_25_q), .in25(register_26_q),
    .in26(register_27_q), .in27(register_28_q), .in28(register_29_q), .in29(register_30_q),
    .in30(register_31_q), .in31(register_32_q), .out(RD2), .sel(A2));

  // Notes on the sheet:
  //   $zero
  //   1
  //   2
  //   3
  //   4
  //   5
  //   6
  //   7
  //   8
  //   9
  //   10
  //   11
  //   12
  //   13
endmodule

module InstructionMemory (
  input  [31:0] A,
  output [31:0] RD
);

  ROM #(.addrWidth(9), .dataWidth(32)) rom_1 (.addr(A[10:2]), .data(RD));

  // Notes on the sheet:
  //   contents of rom_1 (hex, n*v repeats v):
  //   20020005 2003000c 2067fff7 e22025 642824 a42820 10a7000a 64202a 10800001 20050000 e2202a 853820
  //   e23822 ac670044 8c020050 8000011 20020001 ac020054
endmodule

module DataMemory (
  input  [31:0] A,
  input  WE,
  input  CLOCK,
  input  [31:0] WD,
  output [31:0] RD
);

  RAM #(.addrWidth(10), .dataWidth(32), .enables("line"), .\type ("nonvolatile")) ram_1 (
    .addr(A[11:2]), .we(WE), .clk(CLOCK), .din(WD), .dout(RD));
endmodule

module MainDecoder (
  input  [5:0] Opcode,
  output Jump,
  output RegDest,
  output Branch,
  output MemWrite,
  output MemToReg,
  output RegWrite,
  output ALUSrc,
  output [1:0] ALUOp
);

  wire ADDI_out;

  and R_type (ALUOp[1], ~Opcode[5], ~Opcode[4], ~Opcode[3], ~Opcode[2], ~Opcode[1], ~Opcode[0]);  // AND_Gate
  and LW (MemToReg, Opcode[5], ~Opcode[4], ~Opcode[3], ~Opcode[2], Opcode[1], Opcode[0]);  // AND_Gate
  and SW (MemWrite, Opcode[5], ~Opcode[4], Opcode[3], ~Opcode[2], Opcode[1], Opcode[0]);  // AND_Gate
  and BEQ (ALUOp[0], ~Opcode[5], ~Opcode[4], ~Opcode[3], Opcode[2], ~Opcode[1], ~Opcode[0]);  // AND_Gate
  and ADDI (ADDI_out, ~Opcode[5], ~Opcode[4], Opcode[3], ~Opcode[2], ~Opcode[1], ~Opcode[0]);  // AND_Gate
  and J (Jump, ~Opcode[5], ~Opcode[4], ~Opcode[3], ~Opcode[2], Opcode[1], ~Opcode[0]);  // AND_Gate
  or or_1 (RegWrite, ADDI_out, MemToReg, ALUOp[1]);
  nor nor_1 (ALUSrc, ALUOp[0], ALUOp[1]);

  assign Branch = ALUOp[0];
  assign RegDest = ALUOp[1];
endmodule

module ALUDecoder (
  input  [5:0] Funct,
  input  [1:0] ALUOp,
  output [2:0] ALUControl
);

  wire priority_encoder_1_p2, priority_encoder_1_p3, priority_encoder_1_p4, priority_encoder_1_p5,
       priority_encoder_1_p6;
  wire [2:0] priority_encoder_1_p1;

  // Priority_Encoder priority_encoder_1: pin names not known; wires that end beside it: priority_encoder_1_p1, priority_encoder_1_p2, priority_encoder_1_p3, priority_encoder_1_p4, priority_encoder_1_p5, priority_encoder_1_p6
  Multiplexer #(.select(2), .width(3)) multiplexer_1 (
    .in0(3'b010), .in1(3'b110), .in2(priority_encoder_1_p1), .in3(priority_encoder_1_p1), .out(ALUControl),
    .sel(ALUOp));
  and ADD (priority_encoder_1_p4, ~Funct[3], ~Funct[2], ~Funct[1], ~Funct[0]);  // AND_Gate
  and SUB (priority_encoder_1_p5, ~Funct[3], ~Funct[2], Funct[1], ~Funct[0]);  // AND_Gate
  and AND (priority_encoder_1_p2, ~Funct[3], Funct[2], ~Funct[1], ~Funct[0]);  // AND_Gate
  and OR (priority_encoder_1_p3, ~Funct[3], Funct[2], ~Funct[1], Funct[0]);  // AND_Gate
  and SLT (priority_encoder_1_p6, Funct[3], ~Funct[2], Funct[1], ~Funct[0]);  // AND_Gate

  // Notes on the sheet:
  //   SUB
  //   ADD
  //   Funct Decoder
endmodule
