// Logisim project Work.circ as structural Verilog: 7 circuits, main circuit main
module main (
  input  [5:0] OPCODE,
  input  in_2,
  input  in_3,
  input  in_4,
  input  [3:0] in_5,
  input  in_6,
  input  in_7,
  input  in_8,
  input  in_9
);

  wire and_1_out, button_1_out, button_2_out, clock_1_out, ula_1_zero;
  wire [4:0] multiplexer_1_out;
  wire [27:0] bit_extender_1_out, shifter_1_out;
  wire [31:0] adder_1_out, adder_2_out, bit_extender_2_out, multiplexer_2_out, multiplexer_3_out,
       multiplexer_4_out, multiplexer_5_out, ram_1_data, regfile_1_readdata1, regfile_1_readdata2,
       register_1_q, rom_1_data, shifter_2_out, ula_1_out_4;

  Clock clock_1 (.out(clock_1_out));
  Register #(.width(32)) register_1 (
    .D(multiplexer_4_out), .Q(register_1_q), .clk(clock_1_out), .clr(button_1_out));  // open: en
  Button button_1 (.out(button_1_out));
  Button button_2 (.out(button_2_out));
  Adder #(.width(32)) adder_1 (.a(register_1_q), .b(32'h4), .out(adder_1_out));  // open: cin, cout
  // Probe on rom_1_data
  ROM #(.dataWidth(32)) rom_1 (.addr(register_1_q[9:2]), .data(rom_1_data));  // open: sel
  assign bit_extender_1_out = {{2{1'b0}}, rom_1_data[25:0]};  // Bit_Extender bit_extender_1
  Shifter #(.width(28)) shifter_1 (.in(bit_extender_1_out), .\dist (5'b00010), .out(shifter_1_out));
  Multiplexer #(.width(5), .disabled(0), .enable("false")) multiplexer_1 (
    .in0(rom_1_data[20:16]), .in1(rom_1_data[15:11]), .out(multiplexer_1_out), .sel(in_2));
  // Probe on multiplexer_5_out
  REGFILE regfile_1 (
    .ReadReg1(rom_1_data[25:21]), .ReadReg2(rom_1_data[20:16]), .WriteReg(multiplexer_1_out),
    .RegWrite(in_3), .Clock(clock_1_out), .ReadData1(regfile_1_readdata1), .ReadData2(regfile_1_readdata2),
    .WriteData(multiplexer_5_out), .Clear(button_2_out));
  // Probe on bit_extender_2_out
  assign bit_extender_2_out = {{16{1'b0}}, rom_1_data[15:0]};  // Bit_Extender bit_extender_2
  Multiplexer #(.width(32), .disabled(0), .enable("false")) multiplexer_2 (
    .in0(regfile_1_readdata2), .in1(bit_extender_2_out), .out(multiplexer_2_out), .sel(in_4));
  Shifter #(.width(32)) shifter_2 (.in(bit_extender_2_out), .\dist (5'b00010), .out(shifter_2_out));
  Adder #(.width(32)) adder_2 (.a(adder_1_out), .b(shifter_2_out), .out(adder_2_out));  // open: cin, cout
  and and_1 (and_1_out, in_2, ula_1_zero);
  // Probe on regfile_1_readdata1
  ULA ula_1 (
    .out_4(ula_1_out_4), .Zero(ula_1_zero), .in_2(regfile_1_readdata1), .in_3(multiplexer_2_out),
    .ALU_Control(in_5));
  // Probe on multiplexer_2_out
  Multiplexer #(.width(32), .disabled(0), .enable("false")) multiplexer_3 (
    .in0(adder_2_out), .out(multiplexer_3_out), .sel(and_1_out));  // open: in1
  Multiplexer #(.width(32), .enable("false")) multiplexer_4 (
    .in0(multiplexer_3_out), .in1({adder_1_out[31:28], shifter_1_out}), .out(multiplexer_4_out), .sel(in_9));
  // Probe on multiplexer_4_out
  // Probe on ula_1_out_4[9:2]
  RAM #(.dataWidth(32), .bus("separate")) ram_1 (
    .addr(ula_1_out_4[9:2]), .din(regfile_1_readdata2), .data(ram_1_data), .str(in_6), .clk(clock_1_out),
    .ld(in_7));  // open: sel, clr
  Multiplexer #(.width(32), .enable("false")) multiplexer_5 (
    .in0(ula_1_out_4), .in1(ram_1_data), .out(multiplexer_5_out), .sel(in_8));

  // Other names for the same wires on the sheet: AluSrc[3:0] = in_5; Branch = in_4; Jump = in_9; MemRead = in_7;
  //   MemtoReg = in_8; MemWrite = in_6; RegDst = in_2; RegWrite = in_3

  // Notes on the sheet:
  //   OPCODE: bits 31-26
  //   RS: bits 25-21
  //   RT: bits 20-16
  //   RD: bits 15-11
  //   Shamt: bits 10-6
  //   Funct: bits 5-0
  //   OPCODE: bits 31-26
  //   Endereço de salto: bits 25-0
  //   6 bits
  //   5bits
  //   Instruções
  //   Tipo R: OP|RS|RT|RD|Shamt|Function
  //   5bits
  //   5bits
  //   Tipo J: OP|Endereço
  //   6 bits
  //   JTA = (PC + 4)[31:28] || (target << 2)
  //   5bits
  //   26 bits
  //   6 bits
  //   OPCODE: bits 31-26
  //   RS: bits 25-21
  //   RT: bits 20-16
  //   Imediato: bits 15-0
  //   Tipo I: OP|RS|RT|Imediato
  //   6 bits
  //   5bits
  //   5bits
  //   BTA = PC + 4 + (Offset << 2)
  //   16 bits
  //   Restart PC
  //   Reset Register File
  //   Instrução Atual
  //   contents of rom_1 (hex, n*v repeats v):
  //   2008000a 2009000a 1095020
  //   Reg Write Data
  //   PC + 4
  //   Mem Addr
endmodule

module REGFILE (
  input  [4:0] ReadReg1,
  input  [4:0] ReadReg2,
  input  [31:0] WriteData,
  input  [4:0] WriteReg,
  input  RegWrite,
  input  Clock,
  input  Clear,
  output [31:0] ReadData1,
  output [31:0] ReadData2
);

  wire _1, _2, _3, _4, _5, _6, _7, _8, _9, _10, _11, _12, _13, _14, _15, _16, _17, _18, _19, _20, _21, _22,
       _23, _24, _25, _26, _27, _28, _29, _30, _31, _32, decoder_1_out0, decoder_1_out1, decoder_2_out0,
       decoder_2_out1, decoder_2_out2, decoder_2_out3, decoder_3_out0, decoder_3_out1, decoder_3_out2,
       decoder_3_out3;
  wire [31:0] multiplexer_1_out, multiplexer_2_out, multiplexer_3_out, multiplexer_4_out, multiplexer_5_out,
       multiplexer_6_out, multiplexer_7_out, multiplexer_8_out, multiplexer_9_out, multiplexer_10_out,
       multiplexer_11_out, multiplexer_12_out, multiplexer_13_out, multiplexer_14_out, multiplexer_15_out,
       multiplexer_16_out, multiplexer_17_out, multiplexer_18_out, multiplexer_19_out, multiplexer_20_out,
       register_1_q, register_2_q, register_3_q, register_4_q, register_5_q, register_6_q, register_7_q,
       register_9_q, register_10_q, register_11_q, register_12_q, register_13_q, register_14_q,
       register_15_q, register_16_q, register_17_q, register_18_q, register_19_q, register_20_q,
       register_21_q, register_22_q, register_23_q, register_24_q, register_25_q, register_26_q,
       register_27_q, register_28_q, register_29_q, register_30_q, register_31_q, register_32_q;

  LED led_1 (.in(_1));
  LED led_2 (.in(_2));
  LED led_3 (.in(_3));
  LED led_4 (.in(_4));
  LED led_5 (.in(_5));
  LED led_6 (.in(_6));
  LED led_7 (.in(_7));
  LED led_8 (.in(_8));
  LED led_9 (.in(_9));
  LED led_10 (.in(_10));
  LED led_11 (.in(_11));
  LED led_12 (.in(_12));
  LED led_13 (.in(_13));
  LED led_14 (.in(_14));
  LED led_15 (.in(_15));
  LED led_16 (.in(_16));
  LED led_17 (.in(_17));
  LED led_18 (.in(_18));
  LED led_19 (.in(_19));
  LED led_20 (.in(_20));
  LED led_21 (.in(_21));
  LED led_22 (.in(_22));
  LED led_23 (.in(_23));
  LED led_24 (.in(_24));
  LED led_25 (.in(_25));
  LED led_26 (.in(_26));
  LED led_27 (.in(_27));
  LED led_28 (.in(_28));
  LED led_29 (.in(_29));
  LED led_30 (.in(_30));
  LED led_31 (.in(_31));
  LED led_32 (.in(_32));
  Decoder #(.disabled(0)) decoder_1 (.out0(decoder_1_out0), .out1(decoder_1_out1), .sel(WriteReg[4]), .en(RegWrite));
  // Probe on WriteReg
  Decoder #(.select(2), .disabled(0)) decoder_2 (
    .out0(decoder_2_out0), .out1(decoder_2_out1), .out2(decoder_2_out2), .out3(decoder_2_out3),
    .sel(WriteReg[3:2]), .en(decoder_1_out1));
  Decoder #(.select(2), .disabled(0)) decoder_3 (
    .out0(decoder_3_out0), .out1(decoder_3_out1), .out2(decoder_3_out2), .out3(decoder_3_out3),
    .sel(WriteReg[3:2]), .en(decoder_1_out0));
  Decoder #(.select(2), .disabled(0)) decoder_4 (
    .out0(_1), .out1(_2), .out2(_3), .out3(_4), .sel(WriteReg[1:0]), .en(decoder_3_out0));
  Decoder #(.select(2), .disabled(0)) decoder_5 (
    .out0(_5), .out1(_6), .out2(_7), .out3(_8), .sel(WriteReg[1:0]), .en(decoder_3_out1));
  Decoder #(.select(2), .disabled(0)) decoder_6 (
    .out0(_9), .out1(_10), .out2(_11), .out3(_12), .sel(WriteReg[1:0]), .en(decoder_3_out2));
  Decoder #(.select(2), .disabled(0)) decoder_7 (
    .out0(_13), .out1(_14), .out2(_15), .out3(_16), .sel(WriteReg[1:0]), .en(decoder_3_out3));
  Decoder #(.select(2), .disabled(0)) decoder_8 (
    .out0(_17), .out1(_18), .out2(_19), .out3(_20), .sel(WriteReg[1:0]), .en(decoder_2_out0));
  Decoder #(.select(2), .disabled(0)) decoder_9 (
    .out0(_21), .out1(_22), .out2(_23), .out3(_24), .sel(WriteReg[1:0]), .en(decoder_2_out1));
  Decoder #(.select(2), .disabled(0)) decoder_10 (
    .out0(_25), .out1(_26), .out2(_27), .out3(_28), .sel(WriteReg[1:0]), .en(decoder_2_out2));
  Decoder #(.select(2), .disabled(0)) decoder_11 (
    .out0(_29), .out1(_30), .out2(_31), .out3(_32), .sel(WriteReg[1:0]), .en(decoder_2_out3));
  Register #(.width(32)) register_1 (.D(WriteData), .en(_1), .Q(register_1_q), .clk(Clock), .clr(Clear));
  Register #(.width(32)) register_2 (.D(WriteData), .en(_2), .Q(register_2_q), .clk(Clock), .clr(Clear));
  Register #(.width(32)) register_3 (.D(WriteData), .en(_3), .Q(register_3_q), .clk(Clock), .clr(Clear));
  Register #(.width(32)) register_4 (.D(WriteData), .en(_4), .Q(register_4_q), .clk(Clock), .clr(Clear));
  Register #(.width(32)) register_5 (.D(WriteData), .en(_5), .Q(register_5_q), .clk(Clock), .clr(Clear));
  Register #(.width(32)) register_6 (.D(WriteData), .en(_6), .Q(register_6_q), .clk(Clock), .clr(Clear));
  Register #(.width(32)) register_7 (.D(WriteData), .en(_7), .Q(register_7_q), .clk(Clock), .clr(Clear));
  Register #(.width(32)) register_8 (.D(WriteData), .en(_8), .Q(register_7_q), .clk(Clock), .clr(Clear));
  Register #(.width(32)) register_9 (.D(WriteData), .en(_9), .Q(register_9_q), .clk(Clock), .clr(Clear));
  Register #(.width(32)) register_10 (.D(WriteData), .en(_10), .Q(register_10_q), .clk(Clock), .clr(Clear));
  Register #(.width(32)) register_11 (.D(WriteData), .en(_11), .Q(register_11_q), .clk(Clock), .clr(Clear));
  Register #(.width(32)) register_12 (.D(WriteData), .en(_12), .Q(register_12_q), .clk(Clock), .clr(Clear));
  Register #(.width(32)) register_13 (.D(WriteData), .en(_13), .Q(register_13_q), .clk(Clock), .clr(Clear));
  Register #(.width(32)) register_14 (.D(WriteData), .en(_14), .Q(register_14_q), .clk(Clock), .clr(Clear));
  Register #(.width(32)) register_15 (.D(WriteData), .en(_15), .Q(register_15_q), .clk(Clock), .clr(Clear));
  Register #(.width(32)) register_16 (.D(WriteData), .en(_16), .Q(register_16_q), .clk(Clock), .clr(Clear));
  Register #(.width(32)) register_17 (.D(WriteData), .en(_17), .Q(register_17_q), .clk(Clock), .clr(Clear));
  Register #(.width(32)) register_18 (.D(WriteData), .en(_18), .Q(register_18_q), .clk(Clock), .clr(Clear));
  Register #(.width(32)) register_19 (.D(WriteData), .en(_19), .Q(register_19_q), .clk(Clock), .clr(Clear));
  Register #(.width(32)) register_20 (.D(WriteData), .en(_20), .Q(register_20_q), .clk(Clock), .clr(Clear));
  Register #(.width(32)) register_21 (.D(WriteData), .en(_21), .Q(register_21_q), .clk(Clock), .clr(Clear));
  Register #(.width(32)) register_22 (.D(WriteData), .en(_22), .Q(register_22_q), .clk(Clock), .clr(Clear));
  Register #(.width(32)) register_23 (.D(WriteData), .en(_23), .Q(register_23_q), .clk(Clock), .clr(Clear));
  Register #(.width(32)) register_24 (.D(WriteData), .en(_24), .Q(register_24_q), .clk(Clock), .clr(Clear));
  Register #(.width(32)) register_25 (.D(WriteData), .en(_25), .Q(register_25_q), .clk(Clock), .clr(Clear));
  Register #(.width(32)) register_26 (.D(WriteData), .en(_26), .Q(register_26_q), .clk(Clock), .clr(Clear));
  Register #(.width(32)) register_27 (.D(WriteData), .en(_27), .Q(register_27_q), .clk(Clock), .clr(Clear));
  Register #(.width(32)) register_28 (.D(WriteData), .en(_28), .Q(register_28_q), .clk(Clock), .clr(Clear));
  Register #(.width(32)) register_29 (.D(WriteData), .en(_29), .Q(register_29_q), .clk(Clock), .clr(Clear));
  Register #(.width(32)) register_30 (.D(WriteData), .en(_30), .Q(register_30_q), .clk(Clock), .clr(Clear));
  Register #(.width(32)) register_31 (.D(WriteData), .en(_31), .Q(register_31_q), .clk(Clock), .clr(Clear));
  Register #(.width(32)) register_32 (.D(WriteData), .en(_32), .Q(register_32_q), .clk(Clock), .clr(Clear));
  // Probe on ReadReg1
  Multiplexer #(.select(2), .width(32), .disabled(0), .enable("false")) multiplexer_1 (
    .in0(register_1_q), .in1(register_2_q), .in2(register_3_q), .in3(register_4_q), .out(multiplexer_1_out),
    .sel(ReadReg1[1:0]));
  Multiplexer #(.select(2), .width(32), .disabled(0), .enable("false")) multiplexer_2 (
    .in0(register_5_q), .in1(register_6_q), .in2(register_7_q), .in3(register_7_q), .out(multiplexer_2_out),
    .sel(ReadReg1[1:0]));
  Multiplexer #(.select(2), .width(32), .disabled(0), .enable("false")) multiplexer_3 (
    .in0(register_9_q), .in1(register_10_q), .in2(register_11_q), .in3(register_12_q),
    .out(multiplexer_3_out), .sel(ReadReg1[1:0]));
  Multiplexer #(.select(2), .width(32), .disabled(0), .enable("false")) multiplexer_4 (
    .in0(register_13_q), .in1(register_14_q), .in2(register_15_q), .in3(register_16_q),
    .out(multiplexer_4_out), .sel(ReadReg1[1:0]));
  Multiplexer #(.select(2), .width(32), .disabled(0), .enable("false")) multiplexer_5 (
    .in0(register_17_q), .in1(register_18_q), .in2(register_19_q), .in3(register_20_q),
    .out(multiplexer_5_out), .sel(ReadReg1[1:0]));
  Multiplexer #(.select(2), .width(32), .disabled(0), .enable("false")) multiplexer_6 (
    .in0(register_21_q), .in1(register_22_q), .in2(register_23_q), .in3(register_24_q),
    .out(multiplexer_6_out), .sel(ReadReg1[1:0]));
  Multiplexer #(.select(2), .width(32), .disabled(0), .enable("false")) multiplexer_7 (
    .in0(register_25_q), .in1(register_26_q), .in2(register_27_q), .in3(register_28_q),
    .out(multiplexer_7_out), .sel(ReadReg1[1:0]));
  Multiplexer #(.select(2), .width(32), .disabled(0), .enable("false")) multiplexer_8 (
    .in0(register_29_q), .in1(register_30_q), .in2(register_31_q), .in3(register_32_q),
    .out(multiplexer_8_out), .sel(ReadReg1[1:0]));
  // Probe on ReadReg2
  Multiplexer #(.select(2), .width(32), .disabled(0), .enable("false")) multiplexer_9 (
    .in0(register_1_q), .in1(register_2_q), .in2(register_3_q), .in3(register_4_q), .out(multiplexer_9_out),
    .sel(ReadReg2[1:0]));
  Multiplexer #(.select(2), .width(32), .disabled(0), .enable("false")) multiplexer_10 (
    .in0(register_5_q), .in2(register_6_q), .in3(register_7_q), .out(multiplexer_10_out), .sel(ReadReg2[1:0]));  // open: in1
  Multiplexer #(.select(2), .width(32), .disabled(0), .enable("false")) multiplexer_11 (
    .in0(register_9_q), .in1(register_10_q), .in2(register_11_q), .in3(register_12_q),
    .out(multiplexer_11_out), .sel(ReadReg2[1:0]));
  Multiplexer #(.select(2), .width(32), .disabled(0), .enable("false")) multiplexer_12 (
    .in0(register_13_q), .in1(register_14_q), .in2(register_15_q), .in3(register_16_q),
    .out(multiplexer_12_out), .sel(ReadReg2[1:0]));
  Multiplexer #(.select(2), .width(32), .disabled(0), .enable("false")) multiplexer_13 (
    .in0(register_17_q), .in1(register_18_q), .in2(register_19_q), .in3(register_20_q),
    .out(multiplexer_13_out), .sel(ReadReg2[1:0]));
  Multiplexer #(.select(2), .width(32), .disabled(0), .enable("false")) multiplexer_14 (
    .in0(register_21_q), .in1(register_22_q), .in2(register_23_q), .in3(register_24_q),
    .out(multiplexer_14_out), .sel(ReadReg2[1:0]));
  Multiplexer #(.select(2), .width(32), .disabled(0), .enable("false")) multiplexer_15 (
    .in0(register_25_q), .in1(register_26_q), .in2(register_27_q), .in3(register_28_q),
    .out(multiplexer_15_out), .sel(ReadReg2[1:0]));
  Multiplexer #(.select(2), .width(32), .disabled(0), .enable("false")) multiplexer_16 (
    .in0(register_29_q), .in1(register_30_q), .in2(register_31_q), .in3(register_32_q),
    .out(multiplexer_16_out), .sel(ReadReg2[1:0]));
  Multiplexer #(.select(2), .width(32), .disabled(0), .enable("false")) multiplexer_17 (
    .in0(multiplexer_9_out), .in1(multiplexer_1_out), .in2(multiplexer_10_out), .in3(multiplexer_2_out),
    .out(multiplexer_17_out), .sel(ReadReg2[3:2]));
  Multiplexer #(.select(2), .width(32), .enable("false")) multiplexer_18 (
    .in0(multiplexer_11_out), .in1(multiplexer_3_out), .in2(multiplexer_12_out), .in3(multiplexer_4_out),
    .out(multiplexer_18_out), .sel(ReadReg1[3:2]));
  Multiplexer #(.select(2), .width(32), .disabled(0), .enable("false")) multiplexer_19 (
    .in0(multiplexer_13_out), .in1(multiplexer_5_out), .in2(multiplexer_14_out), .in3(multiplexer_6_out),
    .out(multiplexer_19_out), .sel(ReadReg2[3:2]));
  Multiplexer #(.select(2), .width(32), .disabled(0), .enable("false")) multiplexer_20 (
    .in0(multiplexer_15_out), .in1(multiplexer_7_out), .in2(multiplexer_16_out), .in3(multiplexer_8_out),
    .out(multiplexer_20_out), .sel(ReadReg1[3:2]));
  Multiplexer #(.width(32), .disabled(0), .enable("false")) multiplexer_21 (
    .in0(multiplexer_17_out), .in1(multiplexer_19_out), .out(ReadData1), .sel(ReadReg1[4]));
  Multiplexer #(.width(32), .disabled(0), .enable("false")) multiplexer_22 (
    .in0(multiplexer_18_out), .in1(multiplexer_20_out), .out(ReadData2), .sel(ReadReg2[4]));

  // Notes on the sheet:
  //   Index + 1
endmodule

module ULA (
  input  [3:0] ALU_Control,
  input  [31:0] in_2,
  input  [31:0] in_3,
  output [31:0] out_4,
  output Zero
);

  wire comparator_1_lt;
  wire [31:0] adder_1_out, AND_out, multiplexer_1_out, OR_out, subtractor_1_out, xor_1_out;

  assign AND_out = in_2 & in_3;  // AND_Gate AND, 32 bits wide
  assign OR_out = in_2 | in_3;  // OR_Gate OR, 32 bits wide
  Adder #(.width(32)) adder_1 (.a(in_2), .b(in_3), .out(adder_1_out));  // open: cin, cout
  Subtractor #(.width(32)) subtractor_1 (.a(in_2), .b(in_3), .out(subtractor_1_out));  // open: bin, bout
  Comparator #(.width(32), .mode("unsigned")) comparator_1 (.a(in_2), .b(in_3), .lt(comparator_1_lt));  // open: gt, eq
  assign xor_1_out = in_2 ^ in_3;  // XOR_Gate xor_1, 32 bits wide
  Multiplexer #(.width(32), .enable("false")) multiplexer_1 (
    .in0({32{1'b0}}), .in1(32'h1), .out(multiplexer_1_out), .sel(comparator_1_lt));
  Multiplexer #(.select(4), .width(32), .disabled(0), .enable("false")) multiplexer_2 (
    .in0(AND_out), .in1(OR_out), .in2(adder_1_out), .in6(subtractor_1_out), .in7(multiplexer_1_out),
    .in12(xor_1_out), .out(out_4), .sel(ALU_Control));  // open: in3, in4, in5, in8, in9, in10, in11, in13, in14, in15
  Comparator #(.width(32), .mode("unsigned")) comparator_2 (.a(out_4), .b({32{1'b0}}), .eq(Zero));  // open: gt, lt

  // Notes on the sheet:
  //   A
  //   B
  //   NOR
  //   Somador
  //   Subtrator
  //   Comparador
  //   Output
  //   ALU Control seleciona a operação
endmodule

module UNIDADE_DE_CONTROLE (
  input  [5:0] in_1,
  input  [1:0] ALUOp,
  output RegDst,
  output Branch,
  output MemRead,
  output MemtoReg,
  output MemWrite,
  output ALUSrc,
  output RegWrite,
  output Jump
);

  wire instruction_type_decoder_1_addi, instruction_type_decoder_1_beq, instruction_type_decoder_1_jump,
       instruction_type_decoder_1_lw, instruction_type_decoder_1_r_format_48db13f9,
       instruction_type_decoder_1_sw;

  Instruction_Type_Decoder instruction_type_decoder_1 (
    .opcode(in_1), .R_format_48db13f9(instruction_type_decoder_1_r_format_48db13f9),
    .lw(instruction_type_decoder_1_lw), .sw(instruction_type_decoder_1_sw),
    .beq(instruction_type_decoder_1_beq), .addi(instruction_type_decoder_1_addi),
    .jump(instruction_type_decoder_1_jump));
  CONTROL_DECODER control_decoder_1 (
    .Rformat(instruction_type_decoder_1_r_format_48db13f9), .lw(instruction_type_decoder_1_lw),
    .sw(instruction_type_decoder_1_sw), .beq(instruction_type_decoder_1_beq),
    .addi(instruction_type_decoder_1_addi), .jump(instruction_type_decoder_1_jump), .RegDst(RegDst),
    .ALUSrc(ALUSrc), .MemtoReg(MemtoReg), .RegWrite(RegWrite), .MemRead(MemRead), .MemWrite(MemWrite),
    .Branch(Branch), .ALUOp1(ALUOp[1]), .ALUOp0(ALUOp[0]), .jump_2(Jump));

  // Notes on the sheet:
  //   Instruction Opcode
endmodule

module Instruction_Type_Decoder (
  input  [5:0] opcode,
  output R_format_48db13f9,
  output lw,
  output sw,
  output beq,
  output addi,
  output jump
);

  Comparator #(.width(6), .mode("unsigned")) comparator_1 (
    .a({6{1'b0}}), .b(opcode), .eq(R_format_48db13f9));  // open: gt, lt
  Comparator #(.width(6), .mode("unsigned")) comparator_2 (.a(6'b100011), .b(opcode), .eq(lw));  // open: gt, lt
  Comparator #(.width(6), .mode("unsigned")) comparator_3 (.a(6'b101011), .b(opcode), .eq(sw));  // open: gt, lt
  Comparator #(.width(6), .mode("unsigned")) comparator_4 (.a(6'b000100), .b(opcode), .eq(beq));  // open: gt, lt
  Comparator #(.width(6), .mode("unsigned")) comparator_5 (.a(6'b001000), .b(opcode), .eq(addi));  // open: gt, lt
  Comparator #(.width(6), .mode("unsigned")) comparator_6 (.a(6'b000010), .b(opcode), .eq(jump));  // open: gt, lt
endmodule

module CONTROL_DECODER (
  input  Rformat,
  input  lw,
  input  sw,
  input  beq,
  input  addi,
  input  jump,
  output RegDst,
  output ALUSrc,
  output MemtoReg,
  output RegWrite,
  output MemRead,
  output MemWrite,
  output Branch,
  output ALUOp1,
  output ALUOp0,
  output jump_2
);

  wire and_1_out, and_2_out, and_3_out, and_4_out, and_5_out, and_6_out, and_7_out, and_9_out, and_10_out,
       and_11_out, not_1_out, not_2_out, not_3_out, not_4_out, not_5_out, not_6_out, not_7_out, not_8_out,
       not_9_out, not_10_out, not_11_out, not_12_out, not_13_out, not_14_out, not_15_out;

  not not_1 (not_1_out, lw);
  not not_2 (not_2_out, addi);
  not not_3 (not_3_out, lw);
  not not_4 (not_4_out, lw);
  not not_5 (not_5_out, lw);
  not not_6 (not_6_out, Rformat);
  not not_7 (not_7_out, beq);
  not not_8 (not_8_out, Rformat);
  not not_9 (not_9_out, Rformat);
  not not_10 (not_10_out, Rformat);
  not not_11 (not_11_out, sw);
  not not_12 (not_12_out, beq);
  not not_13 (not_13_out, Rformat);
  not not_14 (not_14_out, Rformat);
  not not_15 (not_15_out, Rformat);
  and and_1 (and_1_out, not_1_out, not_2_out);
  and and_2 (and_2_out, not_3_out, beq);
  and and_3 (and_3_out, not_4_out, sw);
  and and_4 (and_4_out, Rformat, not_5_out);
  and and_5 (and_5_out, not_6_out, not_7_out, addi);
  and and_6 (and_6_out, not_8_out, sw);
  and and_7 (and_7_out, not_9_out, lw);
  and and_8 (MemtoReg, not_10_out, lw);
  and and_9 (and_9_out, not_11_out, not_12_out, addi);
  and and_10 (and_10_out, not_13_out, lw);
  and and_11 (and_11_out, lw, sw, beq);
  and and_12 (MemWrite, not_14_out, sw);
  and and_13 (Branch, not_15_out, beq);
  or or_1 (RegDst, and_1_out, and_2_out, and_3_out, and_4_out);
  or or_2 (ALUSrc, and_5_out, and_6_out, and_7_out);
  or or_3 (RegWrite, and_9_out, lw, Rformat);
  or or_4 (MemRead, and_10_out, and_11_out);

  assign ALUOp0 = beq;
  assign ALUOp1 = Rformat;
  assign jump_2 = jump;
endmodule

module ULA_CONTROL (
  input  [5:0] Function,
  input  [1:0] ALUOp,
  output [3:0] Operation
);

  wire A_2_out, A_3_out, A_out, and_1_out, and_2_out, and_3_out, C_out, not_1_out, not_2_out, not_3_out,
       not_4_out, not_5_out, not_6_out, not_7_out, not_8_out, not_9_out, not_10_out, not_11_out, not_12_out,
       not_13_out, not_14_out, not_15_out, not_16_out, not_17_out, not_18_out, not_19_out, not_20_out,
       or_1_out, or_2_out;
  wire [2:0] priority_encoder_1_out;

  not not_1 (not_1_out, ALUOp[1]);
  not not_2 (not_2_out, ALUOp[0]);
  not not_3 (not_3_out, ALUOp[0]);
  not not_4 (not_4_out, Function[3]);
  not not_5 (not_5_out, Function[2]);
  not not_6 (not_6_out, Function[1]);
  not not_7 (not_7_out, Function[0]);
  not not_8 (not_8_out, ALUOp[1]);
  not not_9 (not_9_out, Function[3]);
  not not_10 (not_10_out, Function[2]);
  not not_11 (not_11_out, Function[0]);
  and and_1 (and_1_out, not_1_out, not_2_out);
  and and_2 (and_2_out, ALUOp[1], not_3_out, not_4_out, not_5_out, not_6_out, not_7_out);
  and and_3 (and_3_out, not_8_out, ALUOp[0]);
  and C (C_out, ALUOp[1], not_9_out, not_10_out, Function[1], not_11_out);
  not not_12 (not_12_out, ALUOp[0]);
  not not_13 (not_13_out, Function[3]);
  and A (A_out, ALUOp[1], not_12_out, not_13_out, Function[2], not_14_out, not_15_out);
  not not_14 (not_14_out, Function[1]);
  not not_15 (not_15_out, Function[0]);
  not not_16 (not_16_out, ALUOp[0]);
  not not_17 (not_17_out, Function[3]);
  and A_2 (A_2_out, ALUOp[1], not_16_out, not_17_out, Function[2], not_18_out, Function[0]);
  not not_18 (not_18_out, Function[1]);
  not not_19 (not_19_out, Function[2]);
  and A_3 (A_3_out, ALUOp[1], Function[3], not_19_out, Function[1], not_20_out);
  not not_20 (not_20_out, Function[0]);
  or or_1 (or_1_out, and_1_out, and_2_out);
  or or_2 (or_2_out, and_3_out, C_out);
  Priority_Encoder #(.disabled(0)) priority_encoder_1 (
    .in0(A_out), .in1(A_2_out), .in2(or_1_out), .in3(or_2_out), .in4(A_3_out), .out(priority_encoder_1_out));  // open: in5, in6, in7, en_in, gs, en_out
  Multiplexer #(.select(3), .width(4), .disabled(0)) multiplexer_1 (
    .in0(4'b0000), .in1(4'b0001), .in2(4'b0010), .in3(4'b0110), .in4(4'b0111), .out(Operation),
    .sel(priority_encoder_1_out));  // open: in5, in6, in7, en

  // Notes on the sheet:
  //   Inputs
  //   B -- OR
  //   Dica: Aqui está a lógica para a primeira linha:
  //   A -- if (ALUOp1=0 and ALUOp0=0)
  //   D -- then output = 2 = 0010
  //   A
  //   C
  //   B -- OR
  //   A
  //   A -- if (ALUOP1=1 and ALUOP0=0 and F3, F1 are 0 and F2, F0 are 1) 
  //   A -- if (ALUOp1=1 and F3, F1 are 1 and F2, F0 are 0)
  //   C -- if (ALUOp1=1 and ALUOp0=0 and F3, F2, F1, F0 are all 0)
  //   B
  //   A -- if (ALUOp1=0 and ALUOp0=1)
  //   C -- if (ALUOp1=1 and F1=1 and F3, F2, F0 are all 0)
  //   B
  //   A -- if (ALUOP1=1 and ALUOP0=0 and F2=1 and F3, F1, F0 are all 0) 
  //   True for 0010=2
  //   True for 0110=6
  //   True for 0000=0
  //   True for 0001=1
  //   True for 0111=7
  //   Nós temos 5 possíveis saídas
  //   D
  //   Dependendo de cada entrada é 1
  //   uma das saídas acima será selecionada.
endmodule
