// Logisim project circuito.circ as structural Verilog: 8 circuits, main circuit mips
module alu (
  input  [3:0] ALU_Control,
  input  [31:0] in_2,
  input  [31:0] in_3,
  output [31:0] out_4,
  output Zero
);

  wire comparator_1_lt;
  wire [31:0] adder_1_out, AND_out, multiplexer_1_out, OR_out, subtractor_1_out, xor_1_out;

  assign AND_out = in_2 & in_3;  // AND_Gate AND, 32 bits wide
  assign OR_out = in_2 | in_3;  // OR_Gate OR, 32 bits wide
  Adder #(.width(32)) adder_1 (.a(in_2), .b(in_3), .out(adder_1_out));  // open: cin, cout
  Subtractor #(.width(32)) subtractor_1 (.a(in_2), .b(in_3), .out(subtractor_1_out));  // open: bin, bout
  Comparator #(.width(32), .mode("unsigned")) comparator_1 (.a(in_2), .b(in_3), .lt(comparator_1_lt));  // open: gt, eq
  assign xor_1_out = in_2 ^ in_3;  // XOR_Gate xor_1, 32 bits wide
  Multiplexer #(.width(32), .enable("false")) multiplexer_1 (
    .in0({32{1'b0}}), .in1(32'h1), .out(multiplexer_1_out), .sel(comparator_1_lt));
  Multiplexer #(.select(4), .width(32), .disabled(0), .enable("false")) multiplexer_2 (
    .in0(AND_out), .in1(OR_out), .in2(adder_1_out), .in6(subtractor_1_out), .in7(multiplexer_1_out),
    .in12(xor_1_out), .out(out_4), .sel(ALU_Control));  // open: in3, in4, in5, in8, in9, in10, in11, in13, in14, in15
  Comparator #(.width(32), .mode("unsigned")) comparator_2 (.a(out_4), .b({32{1'b0}}), .eq(Zero));  // open: gt, lt

  // Notes on the sheet:
  //   A
  //   B
  //   NOR
  //   Somador
  //   Subtrator
  //   Comparador
  //   Output
  //   ALU Control seleciona a operação
endmodule

module mips (
  output [3:0] out_1
);

  wire alu_1_zero, AluSrc, and_1_out, Branch, Clear, clock_1_out, Jump, MemRead, MemtoReg, MemWrite,
       PC_reset, RegDst, RegWrite;
  wire [1:0] control_unit_1_out_10;
  wire [4:0] multiplexer_1_out;
  wire [5:0] Function, Opcode;
  wire [7:0] alu_1_out_4_2;
  wire [25:6] rom_1_data;
  wire [27:0] bit_extender_1_out, shifter_1_out;
  wire [31:0] adder_1_out, adder_2_out, alu_1_out_4, bit_extender_2_out, multiplexer_2_out,
       multiplexer_3_out, multiplexer_4_out, multiplexer_5_out, ram_1_data, regfile_1_out_8,
       regfile_1_out_15, regfile_1_out_17, regfile_1_out_28, regfile_1_out_34, regfile_1_read_data_1,
       regfile_1_read_data_2, register_1_q, shifter_2_out;

  Register #(.width(32)) register_1 (
    .D(multiplexer_4_out), .Q(register_1_q), .clk(clock_1_out), .clr(PC_reset));  // open: en
  Clock clock_1 (.out(clock_1_out));
  Button button_1 (.out(PC_reset));
  Adder #(.width(32)) adder_1 (.a(register_1_q), .b(32'h4), .out(adder_1_out));  // open: cin, cout
  // Probe on {Opcode, rom_1_data, Function}
  Button button_2 (.out(Clear));
  ROM #(.dataWidth(32)) rom_1 (.addr(register_1_q[9:2]), .data({Opcode, rom_1_data, Function}));  // open: sel
  assign bit_extender_1_out = {{2{rom_1_data[25]}}, {rom_1_data, Function}};  // Bit_Extender bit_extender_1
  Shifter #(.width(28)) shifter_1 (.in(bit_extender_1_out), .\dist (5'b00010), .out(shifter_1_out));
  Multiplexer #(.width(5), .disabled(0), .enable("false")) multiplexer_1 (
    .in0(rom_1_data[20:16]), .in1(rom_1_data[15:11]), .out(multiplexer_1_out), .sel(RegDst));
  // Probe on multiplexer_5_out
  RegFile regfile_1 (
    .Write_Enable(RegWrite), .Write_Reg(multiplexer_1_out), .Write_Data(multiplexer_5_out),
    .Clock(clock_1_out), .Reset(Clear), .out_8(regfile_1_out_8), .out_11(regfile_1_out_8),
    .out_15(regfile_1_out_15), .out_17(regfile_1_out_17), .out_23(regfile_1_out_17),
    .out_27(regfile_1_out_8), .out_28(regfile_1_out_28), .out_29(regfile_1_out_28),
    .out_34(regfile_1_out_34), .out_35(regfile_1_out_34), .out_39(regfile_1_out_15),
    .Read_Reg_1(rom_1_data[25:21]), .Read_Reg_2(rom_1_data[20:16]), .Read_Data_1(regfile_1_read_data_1),
    .Read_Data_2(regfile_1_read_data_2));  // open: out_10, out_12, out_14, out_16, out_18, out_20, out_22, out_9, out_13, out_19, out_21, out_24, out_25, out_26, out_30, out_31, out_32, out_33, out_36, out_37, out_38
  // Probe on rom_1_data[25:21]
  // Probe on rom_1_data[20:16]
  // Probe on multiplexer_1_out
  assign bit_extender_2_out = {{16{rom_1_data[15]}}, {rom_1_data[15:6], Function}};  // Bit_Extender bit_extender_2
  Shifter #(.width(32)) shifter_2 (.in(bit_extender_2_out), .\dist (5'b00010), .out(shifter_2_out));
  Multiplexer #(.width(32), .enable("false")) multiplexer_2 (
    .in0(regfile_1_read_data_2), .in1(bit_extender_2_out), .out(multiplexer_2_out), .sel(AluSrc));
  // Probe on bit_extender_2_out
  // Probe on regfile_1_read_data_1
  // Probe on multiplexer_2_out
  alu alu_1 (
    .ALU_Control(out_1), .in_2(regfile_1_read_data_1), .in_3(multiplexer_2_out),
    .out_4({alu_1_out_4[31:10], alu_1_out_4_2, alu_1_out_4[1:0]}), .Zero(alu_1_zero));
  Adder #(.width(32)) adder_2 (.a(adder_1_out), .b(shifter_2_out), .out(adder_2_out));  // open: cin, cout
  // Probe on {alu_1_out_4[31:10], alu_1_out_4_2, alu_1_out_4[1:0]}
  Multiplexer #(.width(32), .enable("false")) multiplexer_3 (
    .in0(adder_1_out), .in1(adder_2_out), .out(multiplexer_3_out), .sel(and_1_out));
  and and_1 (and_1_out, Branch, alu_1_zero);
  // Probe on multiplexer_4_out
  Multiplexer #(.width(32), .enable("false")) multiplexer_4 (
    .in0(multiplexer_3_out), .in1({adder_1_out[31:28], shifter_1_out}), .out(multiplexer_4_out), .sel(Jump));
  // Probe on alu_1_out_4_2
  RAM #(.dataWidth(32)) ram_1 (
    .addr(alu_1_out_4_2), .data(ram_1_data), .sel(MemWrite), .clk(clock_1_out), .ld(MemRead));  // open: clr
  Multiplexer #(.width(32), .enable("false")) multiplexer_5 (
    .in0({alu_1_out_4[31:10], alu_1_out_4_2, alu_1_out_4[1:0]}), .in1(ram_1_data), .out(multiplexer_5_out),
    .sel(MemtoReg));
  Control_Unit control_unit_1 (
    .in_1(Opcode), .out_2(RegDst), .out_3(AluSrc), .out_4(MemtoReg), .out_5(RegWrite), .out_6(MemRead),
    .out_7(MemWrite), .out_8(Branch), .out_9(Jump), .out_10(control_unit_1_out_10));
  ALU_Control alu_control_1 (.Function(Function), .ALUOp(control_unit_1_out_10), .Operation(out_1));

  // Other names for the same wires on the sheet: ALU_CODE[3:0] = out_1

  // Notes on the sheet:
  //   Clock
  //   Reset PC
  //   OPCODE: bits 31-26
  //   RS: bits 25-21
  //   RT: bits 20-16
  //   RD: bits 15-11
  //   Shamt: bits 10-6
  //   Funct: bits 5-0
  //   OPCODE: bits 31-26
  //   Endereço de salto: bits 25-0
  //   Current Instruction
  //   Reset RegFile
  //   6 bits
  //   5bits
  //   contents of rom_1 (hex, n*v repeats v):
  //   20020005 2003000c 2067fff7 e22025 642824 a42820 10a70008 64202a 10800001 2005000a e2202a 853820
  //   e23822 ac670044 8c020050 8000011 20020001 ac020054
  //   Tipo R: OP|RS|RT|RD|Shamt|Function
  //   5bits
  //   5bits
  //   Tipo J: OP|Endereço
  //   6 bits
  //   JTA = (PC + 4)[31:28] || (target << 2)
  //   5bits
  //   26 bits
  //   Reg Write Data
  //   6 bits
  //   OPCODE: bits 31-26
  //   RS: bits 25-21
  //   RT: bits 20-16
  //   Imediato: bits 15-0
  //   Tipo I: OP|RS|RT|Imediato
  //   6 bits
  //   5bits
  //   5bits
  //   BTA = PC + 4 + (Offset << 2)
  //   Imm. Value
  //   16 bits
  //   Next PC
  //   Mem Addr
endmodule

module RegFile (
  input  Write_Enable,
  input  [31:0] Write_Data,
  input  [4:0] Write_Reg,
  input  Clock,
  input  Reset,
  input  [4:0] Read_Reg_1,
  input  [4:0] Read_Reg_2,
  output [31:0] out_8,
  output [31:0] out_9,
  output [31:0] out_10,
  output [31:0] out_11,
  output [31:0] out_12,
  output [31:0] out_13,
  output [31:0] out_14,
  output [31:0] out_15,
  output [31:0] out_16,
  output [31:0] out_17,
  output [31:0] out_18,
  output [31:0] out_19,
  output [31:0] out_20,
  output [31:0] out_21,
  output [31:0] out_22,
  output [31:0] out_23,
  output [31:0] out_24,
  output [31:0] out_25,
  output [31:0] out_26,
  output [31:0] out_27,
  output [31:0] out_28,
  output [31:0] out_29,
  output [31:0] out_30,
  output [31:0] out_31,
  output [31:0] out_32,
  output [31:0] out_33,
  output [31:0] out_34,
  output [31:0] out_35,
  output [31:0] out_36,
  output [31:0] out_37,
  output [31:0] out_38,
  output [31:0] out_39,
  output [31:0] Read_Data_1,
  output [31:0] Read_Data_2
);

  wire _1, _2, _3, _4, _5, _6, _7, _8, _9, _10, _11, _12, _13, _14, _15, _16, _17, _18, _19, _20, _21, _22,
       _23, _24, _25, _26, _27, _28, _29, _30, _31, zero;

  Demultiplexer #(.select(5), .disabled(0), .enable("false")) demultiplexer_1 (
    .out0(zero), .out1(_1), .out2(_2), .out3(_3), .out4(_4), .out5(_5), .out6(_6), .out7(_7), .out8(_8),
    .out9(_9), .out10(_10), .out11(_11), .out12(_12), .out13(_13), .out14(_14), .out15(_15), .out16(_16),
    .out17(_17), .out18(_18), .out19(_19), .out20(_20), .out21(_21), .out22(_22), .out23(_23), .out24(_24),
    .out25(_25), .out26(_26), .out27(_27), .out28(_28), .out29(_29), .out30(_30), .out31(_31),
    .in(Write_Enable), .sel(Write_Reg));
  Register #(.width(32)) register_1 (.D(Write_Data), .en(zero), .Q(out_8), .clk(Clock), .clr(Reset));
  Register #(.width(32)) register_2 (.D(Write_Data), .en(_1), .Q(out_10), .clk(Clock), .clr(Reset));
  Register #(.width(32)) register_3 (.D(Write_Data), .en(_2), .Q(out_12), .clk(Clock), .clr(Reset));
  Register #(.width(32)) register_4 (.D(Write_Data), .en(_3), .Q(out_14), .clk(Clock), .clr(Reset));
  Register #(.width(32)) register_5 (.D(Write_Data), .en(_4), .Q(out_16), .clk(Clock), .clr(Reset));
  Register #(.width(32)) register_6 (.D(Write_Data), .en(_5), .Q(out_18), .clk(Clock), .clr(Reset));
  Register #(.width(32)) register_7 (.D(Write_Data), .en(_6), .Q(out_20), .clk(Clock), .clr(Reset));
  Register #(.width(32)) register_8 (.D(Write_Data), .en(_7), .Q(out_22), .clk(Clock), .clr(Reset));
  Register #(.width(32)) register_9 (.D(Write_Data), .en(_16), .Q(out_24), .clk(Clock), .clr(Reset));
  Register #(.width(32)) register_10 (.D(Write_Data), .en(_17), .Q(out_26), .clk(Clock), .clr(Reset));
  Register #(.width(32)) register_11 (.D(Write_Data), .en(_18), .Q(out_28), .clk(Clock), .clr(Reset));
  Register #(.width(32)) register_12 (.D(Write_Data), .en(_19), .Q(out_30), .clk(Clock), .clr(Reset));
  Register #(.width(32)) register_13 (.D(Write_Data), .en(_20), .Q(out_32), .clk(Clock), .clr(Reset));
  Register #(.width(32)) register_14 (.D(Write_Data), .en(_21), .Q(out_34), .clk(Clock), .clr(Reset));
  Register #(.width(32)) register_15 (.D(Write_Data), .en(_22), .Q(out_36), .clk(Clock), .clr(Reset));
  Register #(.width(32)) register_16 (.D(Write_Data), .en(_23), .Q(out_38), .clk(Clock), .clr(Reset));
  Multiplexer #(.select(5), .width(32), .disabled(0), .enable("false")) multiplexer_1 (
    .in0(out_8), .in1(out_10), .in2(out_12), .in3(out_14), .in4(out_16), .in5(out_18), .in6(out_20),
    .in7(out_22), .in8(out_9), .in9(out_11), .in10(out_13), .in11(out_15), .in12(out_17), .in13(out_19),
    .in14(out_21), .in15(out_23), .in16(out_24), .in17(out_26), .in18(out_28), .in19(out_30), .in20(out_32),
    .in21(out_34), .in22(out_36), .in23(out_38), .in24(out_25), .in25(out_27), .in26(out_29), .in27(out_31),
    .in28(out_33), .in29(out_35), .in30(out_37), .in31(out_39), .out(Read_Data_1), .sel(Read_Reg_1));
  Multiplexer #(.select(5), .width(32), .disabled(0), .enable("false")) multiplexer_2 (
    .in0(out_8), .in1(out_10), .in2(out_12), .in3(out_14), .in4(out_16), .in5(out_18), .in6(out_20),
    .in7(out_22), .in8(out_9), .in9(out_11), .in10(out_13), .in11(out_15), .in12(out_17), .in13(out_19),
    .in14(out_21), .in15(out_23), .in16(out_24), .in17(out_26), .in18(out_28), .in19(out_30), .in20(out_32),
    .in21(out_34), .in22(out_36), .in23(out_38), .in24(out_25), .in25(out_27), .in26(out_29), .in27(out_31),
    .in28(out_33), .in29(out_35), .in30(out_37), .in31(out_39), .out(Read_Data_2), .sel(Read_Reg_2));
  Register #(.width(32)) register_17 (.D(Write_Data), .en(_8), .Q(out_9), .clk(Clock), .clr(Reset));
  Register #(.width(32)) register_18 (.D(Write_Data), .en(_9), .Q(out_11), .clk(Clock), .clr(Reset));
  Register #(.width(32)) register_19 (.D(Write_Data), .en(_10), .Q(out_13), .clk(Clock), .clr(Reset));
  Register #(.width(32)) register_20 (.D(Write_Data), .en(_11), .Q(out_15), .clk(Clock), .clr(Reset));
  Register #(.width(32)) register_21 (.D(Write_Data), .en(_12), .Q(out_17), .clk(Clock), .clr(Reset));
  Register #(.width(32)) register_22 (.D(Write_Data), .en(_13), .Q(out_19), .clk(Clock), .clr(Reset));
  Register #(.width(32)) register_23 (.D(Write_Data), .en(_14), .Q(out_21), .clk(Clock), .clr(Reset));
  Register #(.width(32)) register_24 (.D(Write_Data), .en(_15), .Q(out_23), .clk(Clock), .clr(Reset));
  Register #(.width(32)) register_25 (.D(Write_Data), .en(_24), .Q(out_25), .clk(Clock), .clr(Reset));
  Register #(.width(32)) register_26 (.D(Write_Data), .en(_25), .Q(out_27), .clk(Clock), .clr(Reset));
  Register #(.width(32)) register_27 (.D(Write_Data), .en(_26), .Q(out_29), .clk(Clock), .clr(Reset));
  Register #(.width(32)) register_28 (.D(Write_Data), .en(_27), .Q(out_31), .clk(Clock), .clr(Reset));
  Register #(.width(32)) register_29 (.D(Write_Data), .Q(out_33), .clk(Clock), .clr(Reset));  // open: en
  Register #(.width(32)) register_30 (.D(Write_Data), .en(_29), .Q(out_35), .clk(Clock), .clr(Reset));
  Register #(.width(32)) register_31 (.D(Write_Data), .en(_30), .Q(out_37), .clk(Clock), .clr(Reset));
  Register #(.width(32)) register_32 (.D(Write_Data), .en(_31), .Q(out_39), .clk(Clock), .clr(Reset));

  // Other names for the same wires on the sheet: _0[31:0] = out_8; _1_t[31:0] = out_10; _2_t[31:0] = out_12;
  //   _3_t[31:0] = out_14; _4_t[31:0] = out_16; _5_t[31:0] = out_18; _6_t[31:0] = out_20; _7_t[31:0] = out_22;
  //   _8_t[31:0] = out_9; _9_t[31:0] = out_11; _10_t[31:0] = out_13; _11_t[31:0] = out_15; _12_t[31:0] = out_17;
  //   _13_t[31:0] = out_19; _14_t[31:0] = out_21; _15_t[31:0] = out_23; _16_t[31:0] = out_24; _17_t[31:0] = out_26;
  //   _18_t[31:0] = out_28; _19_t[31:0] = out_30; _20_t[31:0] = out_32; _21_t[31:0] = out_34; _22_t[31:0] = out_36;
  //   _23_t[31:0] = out_38; _24_t[31:0] = out_25; _25_t[31:0] = out_27; _26_t[31:0] = out_29; _27_t[31:0] = out_31;
  //   _28_t[31:0] = out_33; _29_t[31:0] = out_35; _30_t[31:0] = out_37; _31_t[31:0] = out_39; Data[31:0] = Write_Data
endmodule

module Instruction_Type_Decoder (
  input  [5:0] opcode,
  output Tipo_R_Formato,
  output lw,
  output sw,
  output beq,
  output addi,
  output jump
);

  Comparator #(.width(6), .mode("unsigned")) comparator_1 (
    .a({6{1'b0}}), .b(opcode), .eq(Tipo_R_Formato));  // open: gt, lt
  Comparator #(.width(6), .mode("unsigned")) comparator_2 (.a(6'b100011), .b(opcode), .eq(lw));  // open: gt, lt
  Comparator #(.width(6), .mode("unsigned")) comparator_3 (.a(6'b101011), .b(opcode), .eq(sw));  // open: gt, lt
  Comparator #(.width(6), .mode("unsigned")) comparator_4 (.a(6'b000100), .b(opcode), .eq(beq));  // open: gt, lt
  Comparator #(.width(6), .mode("unsigned")) comparator_5 (.a(6'b001000), .b(opcode), .eq(addi));  // open: gt, lt
  Comparator #(.width(6), .mode("unsigned")) comparator_6 (.a(6'b000010), .b(opcode), .eq(jump));  // open: gt, lt
endmodule

module Control_Decoder (
  input  Rformat,
  input  lw,
  input  sw,
  input  beq,
  input  addi,
  input  jump,
  output RegDst,
  output ALUSrc,
  output MemtoReg,
  output RegWrite,
  output MemRead,
  output MemWrite,
  output Branch,
  output ALUOp1,
  output ALUOp0,
  output jump_2
);

  wire and_1_out, and_2_out, and_3_out, and_4_out, and_5_out, and_6_out, and_7_out, and_9_out, and_10_out,
       and_11_out, not_1_out, not_2_out, not_3_out, not_4_out, not_5_out, not_6_out, not_7_out, not_8_out,
       not_9_out, not_10_out, not_11_out, not_12_out, not_13_out, not_14_out, not_15_out;

  not not_1 (not_1_out, lw);
  not not_2 (not_2_out, addi);
  not not_3 (not_3_out, lw);
  not not_4 (not_4_out, lw);
  not not_5 (not_5_out, lw);
  not not_6 (not_6_out, Rformat);
  not not_7 (not_7_out, beq);
  not not_8 (not_8_out, Rformat);
  not not_9 (not_9_out, Rformat);
  not not_10 (not_10_out, Rformat);
  not not_11 (not_11_out, sw);
  not not_12 (not_12_out, beq);
  not not_13 (not_13_out, Rformat);
  not not_14 (not_14_out, Rformat);
  not not_15 (not_15_out, Rformat);
  and and_1 (and_1_out, not_1_out, not_2_out);
  and and_2 (and_2_out, not_3_out, beq);
  and and_3 (and_3_out, not_4_out, sw);
  and and_4 (and_4_out, Rformat, not_5_out);
  and and_5 (and_5_out, not_6_out, not_7_out, addi);
  and and_6 (and_6_out, not_8_out, sw);
  and and_7 (and_7_out, not_9_out, lw);
  and and_8 (MemtoReg, not_10_out, lw);
  and and_9 (and_9_out, not_11_out, not_12_out, addi);
  and and_10 (and_10_out, not_13_out, lw);
  and and_11 (and_11_out, lw, sw, beq);
  and and_12 (MemWrite, not_14_out, sw);
  and and_13 (Branch, not_15_out, beq);
  or or_1 (RegDst, and_1_out, and_2_out, and_3_out, and_4_out);
  or or_2 (ALUSrc, and_5_out, and_6_out, and_7_out);
  or or_3 (RegWrite, and_9_out, lw, Rformat);
  or or_4 (MemRead, and_10_out, and_11_out);

  assign ALUOp0 = beq;
  assign ALUOp1 = Rformat;
  assign jump_2 = jump;
endmodule

module ALU_Control (
  input  [5:0] Function,
  input  [1:0] ALUOp,
  output [3:0] Operation
);

  wire A_2_out, A_3_out, A_out, and_1_out, and_2_out, and_3_out, C_out, not_1_out, not_2_out, not_3_out,
       not_4_out, not_5_out, not_6_out, not_7_out, not_8_out, not_9_out, not_10_out, not_11_out, not_12_out,
       not_13_out, not_14_out, not_15_out, not_16_out, not_17_out, not_18_out, not_19_out, not_20_out,
       or_1_out, or_2_out;
  wire [2:0] priority_encoder_1_out;

  not not_1 (not_1_out, ALUOp[1]);
  not not_2 (not_2_out, ALUOp[0]);
  not not_3 (not_3_out, ALUOp[0]);
  not not_4 (not_4_out, Function[3]);
  not not_5 (not_5_out, Function[2]);
  not not_6 (not_6_out, Function[1]);
  not not_7 (not_7_out, Function[0]);
  not not_8 (not_8_out, ALUOp[1]);
  not not_9 (not_9_out, Function[3]);
  not not_10 (not_10_out, Function[2]);
  not not_11 (not_11_out, Function[0]);
  and and_1 (and_1_out, not_1_out, not_2_out);
  and and_2 (and_2_out, ALUOp[1], not_3_out, not_4_out, not_5_out, not_6_out, not_7_out);
  and and_3 (and_3_out, not_8_out, ALUOp[0]);
  and C (C_out, ALUOp[1], not_9_out, not_10_out, Function[1], not_11_out);
  not not_12 (not_12_out, ALUOp[0]);
  not not_13 (not_13_out, Function[3]);
  and A (A_out, ALUOp[1], not_12_out, not_13_out, Function[2], not_14_out, not_15_out);
  not not_14 (not_14_out, Function[1]);
  not not_15 (not_15_out, Function[0]);
  not not_16 (not_16_out, ALUOp[0]);
  not not_17 (not_17_out, Function[3]);
  and A_2 (A_2_out, ALUOp[1], not_16_out, not_17_out, Function[2], not_18_out, Function[0]);
  not not_18 (not_18_out, Function[1]);
  not not_19 (not_19_out, Function[2]);
  and A_3 (A_3_out, ALUOp[1], Function[3], not_19_out, Function[1], not_20_out);
  not not_20 (not_20_out, Function[0]);
  or or_1 (or_1_out, and_1_out, and_2_out);
  or or_2 (or_2_out, and_3_out, C_out);
  Priority_Encoder #(.disabled(0)) priority_encoder_1 (
    .in0(A_out), .in1(A_2_out), .in2(or_1_out), .in3(or_2_out), .in4(A_3_out), .out(priority_encoder_1_out));  // open: in5, in6, in7, en_in, gs, en_out
  Multiplexer #(.select(3), .width(4), .disabled(0)) multiplexer_1 (
    .in0(4'b0000), .in1(4'b0001), .in2(4'b0010), .in3(4'b0110), .in4(4'b0111), .out(Operation),
    .sel(priority_encoder_1_out));  // open: in5, in6, in7, en

  // Notes on the sheet:
  //   Inputs
  //   B -- OR
  //   Dica: Aqui está a lógica para a primeira linha:
  //   A -- if (ALUOp1=0 and ALUOp0=0)
  //   D -- then output = 2 = 0010
  //   A
  //   C
  //   B -- OR
  //   A
  //   A -- if (ALUOP1=1 and ALUOP0=0 and F3, F1 are 0 and F2, F0 are 1) 
  //   A -- if (ALUOp1=1 and F3, F1 are 1 and F2, F0 are 0)
  //   C -- if (ALUOp1=1 and ALUOp0=0 and F3, F2, F1, F0 are all 0)
  //   B
  //   A -- if (ALUOp1=0 and ALUOp0=1)
  //   C -- if (ALUOp1=1 and F1=1 and F3, F2, F0 are all 0)
  //   B
  //   A -- if (ALUOP1=1 and ALUOP0=0 and F2=1 and F3, F1, F0 are all 0) 
  //   True for 0010=2
  //   True for 0110=6
  //   True for 0000=0
  //   True for 0001=1
  //   True for 0111=7
  //   Nós temos 5 possíveis saídas
  //   D
  //   Dependendo de cada entrada é 1
  //   uma das saídas acima será selecionada.
endmodule

module Control_Unit (
  input  [5:0] in_1,
  output out_2,
  output out_3,
  output out_4,
  output out_5,
  output out_6,
  output out_7,
  output out_8,
  output out_9,
  output [1:0] out_10
);

  wire instruction_type_decoder_1_addi, instruction_type_decoder_1_beq, instruction_type_decoder_1_jump,
       instruction_type_decoder_1_lw, instruction_type_decoder_1_sw,
       instruction_type_decoder_1_tipo_r_formato;

  Instruction_Type_Decoder instruction_type_decoder_1 (
    .opcode(in_1), .Tipo_R_Formato(instruction_type_decoder_1_tipo_r_formato),
    .lw(instruction_type_decoder_1_lw), .sw(instruction_type_decoder_1_sw),
    .beq(instruction_type_decoder_1_beq), .addi(instruction_type_decoder_1_addi),
    .jump(instruction_type_decoder_1_jump));
  Control_Decoder control_decoder_1 (
    .Rformat(instruction_type_decoder_1_tipo_r_formato), .lw(instruction_type_decoder_1_lw), .RegDst(out_2),
    .sw(instruction_type_decoder_1_sw), .beq(instruction_type_decoder_1_beq),
    .addi(instruction_type_decoder_1_addi), .jump(instruction_type_decoder_1_jump), .ALUSrc(out_3),
    .MemtoReg(out_4), .RegWrite(out_5), .MemRead(out_6), .MemWrite(out_7), .Branch(out_8),
    .ALUOp1(out_10[0]), .ALUOp0(out_10[1]), .jump_2(out_9));
endmodule

module Unidade_de_Controle (
  input  [5:0] Opcode,
  output Jump,
  output RegDest,
  output Branch,
  output Memory_Write,
  output Memory_to_Register,
  output Register_Write,
  output ALUSrc,
  output [1:0] ALUOp
);

  wire ADDI_out;

  and R_Type (ALUOp[1], ~Opcode[5], ~Opcode[4], ~Opcode[3], ~Opcode[2], ~Opcode[1], ~Opcode[0]);  // AND_Gate
  and LW (Memory_to_Register, Opcode[5], ~Opcode[4], ~Opcode[3], ~Opcode[2], Opcode[1], Opcode[0]);  // AND_Gate
  and SW (Memory_Write, Opcode[5], ~Opcode[4], Opcode[3], ~Opcode[2], Opcode[1], Opcode[0]);  // AND_Gate
  and BEQ (ALUOp[0], ~Opcode[5], ~Opcode[4], ~Opcode[3], Opcode[2], ~Opcode[1], ~Opcode[0]);  // AND_Gate
  and ADDI (ADDI_out, ~Opcode[5], ~Opcode[4], Opcode[3], ~Opcode[2], ~Opcode[1], ~Opcode[0]);  // AND_Gate
  and u_JUMP (Jump, ~Opcode[5], ~Opcode[4], ~Opcode[3], ~Opcode[2], Opcode[1], ~Opcode[0]);  // AND_Gate
  or OR (Register_Write, ADDI_out, Memory_to_Register, ALUOp[1]);
  nor NOR (ALUSrc, ALUOp[0], ALUOp[1]);

  assign Branch = ALUOp[0];
  assign RegDest = ALUOp[1];
endmodule
