// Logisim project Trabalho.circ as structural Verilog
module main (
);

  REGFILE regfile_1 ();  // open: ReadReg1, ReadReg2, WriteReg, RegWrite, ReadData1, ReadData2, WriteData, Clk, Reset
  ULA ula_1 ();  // open: out_4, Zero, in_2, in_3, ALU_Control
endmodule

module ULA (
  input  [3:0] ALU_Control,
  input  [31:0] in_2,
  input  [31:0] in_3,
  output [31:0] out_4,
  output Zero
);

  wire comparator_1_lt;
  wire [31:0] adder_1_out, and_1_out, multiplexer_1_out, or_1_out, subtractor_1_out, xor_1_out;

  assign and_1_out = in_2 & in_3;  // AND_Gate and_1, 32 bits wide
  assign or_1_out = in_2 | in_3;  // OR_Gate or_1, 32 bits wide
  Adder #(.width(32)) adder_1 (.a(in_2), .b(in_3), .out(adder_1_out));  // open: cin, cout
  Subtractor #(.width(32)) subtractor_1 (.a(in_2), .b(in_3), .out(subtractor_1_out));  // open: bin, bout
  Comparator #(.width(32), .mode("unsigned")) comparator_1 (.a(in_2), .b(in_3), .lt(comparator_1_lt));  // open: gt, eq
  assign xor_1_out = in_2 ^ in_3;  // XOR_Gate xor_1, 32 bits wide
  Multiplexer #(.width(32), .enable("false")) multiplexer_1 (
    .in0({32{1'b0}}), .in1(32'h1), .out(multiplexer_1_out), .sel(comparator_1_lt));
  Multiplexer #(.select(4), .width(32), .enable("false")) multiplexer_2 (
    .in0(and_1_out), .in1(or_1_out), .in2(adder_1_out), .in6(subtractor_1_out), .in7(multiplexer_1_out),
    .in12(xor_1_out), .out(out_4), .sel(ALU_Control));  // open: in3, in4, in5, in8, in9, in10, in11, in13, in14, in15
  Comparator #(.width(32), .mode("unsigned")) comparator_2 (.a(out_4), .b({32{1'b0}}), .eq(Zero));  // open: gt, lt

  // Notes on the sheet:
  //   A
  //   B
  //   Op selects the result
  //   Output
endmodule

module REGFILE (
  input  [4:0] ReadReg1,
  input  [4:0] ReadReg2,
  input  [4:0] WriteReg,
  input  Clk,
  input  [31:0] WriteData,
  input  RegWrite,
  input  Reset,
  output [31:0] ReadData1,
  output [31:0] ReadData2
);

  wire decoder_1_out0, decoder_1_out1, decoder_2_out0, decoder_2_out1, decoder_2_out2, decoder_2_out3,
       decoder_3_out0, decoder_3_out1, decoder_3_out2, decoder_3_out3, decoder_4_out0, decoder_4_out1,
       decoder_4_out2, decoder_4_out3, decoder_5_out0, decoder_5_out1, decoder_5_out2, decoder_5_out3,
       decoder_6_out0, decoder_6_out1, decoder_6_out2, decoder_7_out0, decoder_7_out1, decoder_7_out2,
       decoder_7_out3, decoder_8_out0, decoder_8_out1, decoder_8_out2, decoder_8_out3, decoder_9_out0,
       decoder_9_out1, decoder_9_out2, decoder_9_out3, decoder_10_out0, decoder_10_out1, decoder_10_out2,
       decoder_10_out3, decoder_11_out0, decoder_11_out1, decoder_11_out2, decoder_11_out3;
  wire [31:0] multiplexer_1_out, multiplexer_2_out, multiplexer_3_out, multiplexer_4_out, multiplexer_5_out,
       multiplexer_6_out, multiplexer_7_out, multiplexer_8_out, multiplexer_9_out, multiplexer_10_out,
       multiplexer_11_out, multiplexer_12_out, multiplexer_13_out, multiplexer_14_out, multiplexer_15_out,
       multiplexer_17_out, multiplexer_18_out, multiplexer_19_out, multiplexer_20_out, register_1_q,
       register_2_q, register_3_q, register_4_q, register_5_q, register_6_q, register_7_q, register_8_q,
       register_9_q, register_10_q, register_11_q, register_12_q, register_13_q, register_14_q,
       register_15_q, register_16_q, register_17_q, register_18_q, register_19_q, register_20_q,
       register_21_q, register_22_q, register_23_q, register_24_q, register_25_q, register_26_q,
       register_27_q, register_28_q, register_29_q, register_30_q, register_31_q, register_32_q;

  LED led_1 (.in(decoder_4_out0));
  LED led_2 (.in(decoder_4_out1));
  LED led_3 (.in(decoder_4_out2));
  LED led_4 (.in(decoder_4_out3));
  LED led_5 (.in(decoder_5_out0));
  LED led_6 (.in(decoder_5_out1));
  LED led_7 (.in(decoder_5_out2));
  LED led_8 (.in(decoder_5_out3));
  LED led_9 (.in(decoder_6_out0));
  LED led_10 (.in(decoder_6_out1));
  LED led_11 (.in(decoder_6_out2));
  LED led_12 (.in(decoder_6_out2));
  LED led_13 (.in(decoder_7_out0));
  LED led_14 (.in(decoder_7_out1));
  LED led_15 (.in(decoder_7_out2));
  LED led_16 (.in(decoder_7_out3));
  LED led_17 (.in(decoder_8_out0));
  LED led_18 (.in(decoder_8_out1));
  LED led_19 (.in(decoder_8_out2));
  LED led_20 (.in(decoder_8_out3));
  LED led_21 (.in(decoder_9_out0));
  LED led_22 (.in(decoder_9_out1));
  LED led_23 (.in(decoder_9_out2));
  LED led_24 (.in(decoder_9_out3));
  LED led_25 (.in(decoder_10_out0));
  LED led_26 (.in(decoder_10_out1));
  LED led_27 (.in(decoder_10_out2));
  LED led_28 (.in(decoder_10_out3));
  LED led_29 (.in(decoder_11_out0));
  LED led_30 (.in(decoder_11_out1));
  LED led_31 (.in(decoder_11_out2));
  LED led_32 (.in(decoder_11_out3));
  // Probe on WriteReg
  Decoder decoder_1 (.out0(decoder_1_out0), .out1(decoder_1_out1), .sel(WriteReg[4]), .en(RegWrite));
  Decoder #(.select(2)) decoder_2 (
    .out0(decoder_2_out0), .out1(decoder_2_out1), .out2(decoder_2_out2), .out3(decoder_2_out3),
    .sel(WriteReg[3:2]), .en(decoder_1_out0));
  Decoder #(.select(2)) decoder_3 (
    .out0(decoder_3_out0), .out1(decoder_3_out1), .out2(decoder_3_out2), .out3(decoder_3_out3),
    .sel(WriteReg[3:2]), .en(decoder_1_out1));
  Decoder #(.select(2)) decoder_4 (
    .out0(decoder_4_out0), .out1(decoder_4_out1), .out2(decoder_4_out2), .out3(decoder_4_out3),
    .sel(WriteReg[1:0]), .en(decoder_2_out0));
  Decoder #(.select(2)) decoder_5 (
    .out0(decoder_5_out0), .out1(decoder_5_out1), .out2(decoder_5_out2), .out3(decoder_5_out3),
    .sel(WriteReg[1:0]), .en(decoder_2_out1));
  Decoder #(.select(2)) decoder_6 (
    .out0(decoder_6_out0), .out1(decoder_6_out1), .out2(decoder_6_out2), .out3(decoder_6_out2),
    .sel(WriteReg[1:0]), .en(decoder_2_out2));
  Decoder #(.select(2)) decoder_7 (
    .out0(decoder_7_out0), .out1(decoder_7_out1), .out2(decoder_7_out2), .out3(decoder_7_out3),
    .sel(WriteReg[1:0]), .en(decoder_2_out3));
  Decoder #(.select(2)) decoder_8 (
    .out0(decoder_8_out0), .out1(decoder_8_out1), .out2(decoder_8_out2), .out3(decoder_8_out3),
    .sel(WriteReg[1:0]), .en(decoder_3_out0));
  Decoder #(.select(2)) decoder_9 (
    .out0(decoder_9_out0), .out1(decoder_9_out1), .out2(decoder_9_out2), .out3(decoder_9_out3),
    .sel(WriteReg[1:0]), .en(decoder_3_out1));
  Decoder #(.select(2)) decoder_10 (
    .out0(decoder_10_out0), .out1(decoder_10_out1), .out2(decoder_10_out2), .out3(decoder_10_out3),
    .sel(WriteReg[1:0]), .en(decoder_3_out2));
  Decoder #(.select(2)) decoder_11 (
    .out0(decoder_11_out0), .out1(decoder_11_out1), .out2(decoder_11_out2), .out3(decoder_11_out3),
    .sel(WriteReg[1:0]), .en(decoder_3_out3));
  Register #(.width(32)) register_1 (.D(WriteData), .en(decoder_4_out0), .clk(Clk), .Q(register_1_q), .clr(Reset));
  Register #(.width(32)) register_2 (.D(WriteData), .en(decoder_4_out1), .clk(Clk), .Q(register_2_q), .clr(Reset));
  Register #(.width(32)) register_3 (.D(WriteData), .en(decoder_4_out2), .clk(Clk), .Q(register_3_q), .clr(Reset));
  Register #(.width(32)) register_4 (.D(WriteData), .en(decoder_4_out3), .clk(Clk), .Q(register_4_q), .clr(Reset));
  Register #(.width(32)) register_5 (.D(WriteData), .en(decoder_5_out0), .clk(Clk), .Q(register_5_q), .clr(Reset));
  Register #(.width(32)) register_6 (.D(WriteData), .en(decoder_5_out1), .clk(Clk), .Q(register_6_q), .clr(Reset));
  Register #(.width(32)) register_7 (.D(WriteData), .en(decoder_5_out2), .clk(Clk), .Q(register_7_q), .clr(Reset));
  Register #(.width(32)) register_8 (.D(WriteData), .en(decoder_5_out3), .clk(Clk), .Q(register_8_q), .clr(Reset));
  Register #(.width(32)) register_9 (.D(WriteData), .en(decoder_6_out0), .clk(Clk), .Q(register_9_q), .clr(Reset));
  Register #(.width(32)) register_10 (.D(WriteData), .en(decoder_6_out1), .clk(Clk), .Q(register_10_q), .clr(Reset));
  Register #(.width(32)) register_11 (.D(WriteData), .en(decoder_6_out2), .clk(Clk), .Q(register_11_q), .clr(Reset));
  Register #(.width(32)) register_12 (.D(WriteData), .en(decoder_6_out2), .clk(Clk), .Q(register_12_q), .clr(Reset));
  Register #(.width(32)) register_13 (.D(WriteData), .en(decoder_7_out0), .clk(Clk), .Q(register_13_q), .clr(Reset));
  Register #(.width(32)) register_14 (.D(WriteData), .en(decoder_7_out1), .clk(Clk), .Q(register_14_q), .clr(Reset));
  Register #(.width(32)) register_15 (.D(WriteData), .en(decoder_7_out2), .clk(Clk), .Q(register_15_q), .clr(Reset));
  Register #(.width(32)) register_16 (.D(WriteData), .en(decoder_7_out3), .clk(Clk), .Q(register_16_q), .clr(Reset));
  Register #(.width(32)) register_17 (.D(WriteData), .en(decoder_8_out0), .clk(Clk), .Q(register_17_q), .clr(Reset));
  Register #(.width(32)) register_18 (.D(WriteData), .en(decoder_8_out1), .clk(Clk), .Q(register_18_q), .clr(Reset));
  Register #(.width(32)) register_19 (.D(WriteData), .en(decoder_8_out2), .clk(Clk), .Q(register_19_q), .clr(Reset));
  Register #(.width(32)) register_20 (.D(WriteData), .en(decoder_8_out3), .clk(Clk), .Q(register_20_q), .clr(Reset));
  Register #(.width(32)) register_21 (.D(WriteData), .en(decoder_9_out0), .clk(Clk), .Q(register_21_q), .clr(Reset));
  Register #(.width(32)) register_22 (.D(WriteData), .en(decoder_9_out1), .clk(Clk), .Q(register_22_q), .clr(Reset));
  Register #(.width(32)) register_23 (.D(WriteData), .en(decoder_9_out2), .clk(Clk), .Q(register_23_q), .clr(Reset));
  Register #(.width(32)) register_24 (.D(WriteData), .en(decoder_9_out3), .clk(Clk), .Q(register_24_q), .clr(Reset));
  Register #(.width(32)) register_25 (.D(WriteData), .en(decoder_10_out0), .clk(Clk), .Q(register_25_q), .clr(Reset));
  Register #(.width(32)) register_26 (.D(WriteData), .en(decoder_10_out1), .clk(Clk), .Q(register_26_q), .clr(Reset));
  Register #(.width(32)) register_27 (.D(WriteData), .en(decoder_10_out2), .clk(Clk), .Q(register_27_q), .clr(Reset));
  Register #(.width(32)) register_28 (.D(WriteData), .en(decoder_10_out3), .clk(Clk), .Q(register_28_q), .clr(Reset));
  Register #(.width(32)) register_29 (.D(WriteData), .en(decoder_11_out0), .clk(Clk), .Q(register_29_q), .clr(Reset));
  Register #(.width(32)) register_30 (.D(WriteData), .en(decoder_11_out1), .clk(Clk), .Q(register_30_q), .clr(Reset));
  Register #(.width(32)) register_31 (.D(WriteData), .en(decoder_11_out2), .clk(Clk), .Q(register_31_q), .clr(Reset));
  Register #(.width(32)) register_32 (.D(WriteData), .en(decoder_11_out3), .clk(Clk), .Q(register_32_q), .clr(Reset));
  // Probe on ReadReg1
  Multiplexer #(.select(2), .width(32), .enable("false")) multiplexer_1 (
    .in0(register_1_q), .in1(register_2_q), .in2(register_3_q), .in3(register_4_q), .out(multiplexer_1_out),
    .sel(ReadReg1[1:0]));
  Multiplexer #(.select(2), .width(32), .enable("false")) multiplexer_2 (
    .in0(register_5_q), .in1(register_6_q), .in2(register_7_q), .in3(register_8_q), .out(multiplexer_2_out),
    .sel(ReadReg1[1:0]));
  Multiplexer #(.select(2), .width(32), .enable("false")) multiplexer_3 (
    .in0(register_9_q), .in1(register_10_q), .in2(register_11_q), .in3(register_12_q),
    .out(multiplexer_3_out), .sel(ReadReg1[1:0]));
  Multiplexer #(.select(2), .width(32), .enable("false")) multiplexer_4 (
    .in0(register_13_q), .in1(register_14_q), .in2(register_15_q), .in3(register_16_q),
    .out(multiplexer_4_out), .sel(ReadReg1[1:0]));
  Multiplexer #(.select(2), .width(32), .enable("false")) multiplexer_5 (
    .in0(register_17_q), .in1(register_18_q), .in2(register_19_q), .in3(register_20_q),
    .out(multiplexer_5_out), .sel(ReadReg1[1:0]));
  Multiplexer #(.select(2), .width(32), .enable("false")) multiplexer_6 (
    .in0(register_21_q), .in1(register_22_q), .in2(register_23_q), .in3(register_24_q),
    .out(multiplexer_6_out), .sel(ReadReg1[1:0]));
  Multiplexer #(.select(2), .width(32), .enable("false")) multiplexer_7 (
    .in0(register_25_q), .in1(register_26_q), .in2(register_27_q), .in3(register_28_q),
    .out(multiplexer_7_out), .sel(ReadReg1[1:0]));
  Multiplexer #(.select(2), .width(32), .enable("false")) multiplexer_8 (
    .in0(register_29_q), .in1(register_30_q), .in2(register_31_q), .in3(register_32_q),
    .out(multiplexer_8_out), .sel(ReadReg1[1:0]));
  // Probe on ReadReg2
  Multiplexer #(.select(2), .width(32), .enable("false")) multiplexer_9 (
    .in0(register_1_q), .in1(register_2_q), .in2(register_3_q), .in3(register_4_q), .out(multiplexer_9_out),
    .sel(ReadReg2[1:0]));
  Multiplexer #(.select(2), .width(32), .enable("false")) multiplexer_10 (
    .in0(register_5_q), .in1(register_6_q), .in2(register_7_q), .in3(register_8_q), .out(multiplexer_10_out),
    .sel(ReadReg2[1:0]));
  Multiplexer #(.select(2), .width(32), .enable("false")) multiplexer_11 (
    .in0(register_9_q), .in1(register_10_q), .in2(register_11_q), .in3(register_12_q),
    .out(multiplexer_11_out), .sel(ReadReg2[1:0]));
  Multiplexer #(.select(2), .width(32), .enable("false")) multiplexer_12 (
    .in0(register_13_q), .in1(register_14_q), .in2(register_15_q), .in3(register_16_q),
    .out(multiplexer_12_out), .sel(ReadReg2[1:0]));
  Multiplexer #(.select(2), .width(32), .enable("false")) multiplexer_13 (
    .in0(register_17_q), .in1(register_18_q), .in2(register_19_q), .in3(register_20_q),
    .out(multiplexer_13_out), .sel(ReadReg2[1:0]));
  Multiplexer #(.select(2), .width(32), .enable("false")) multiplexer_14 (
    .in0(register_21_q), .in1(register_22_q), .in2(register_23_q), .in3(register_24_q),
    .out(multiplexer_14_out), .sel(ReadReg2[1:0]));
  Multiplexer #(.select(2), .width(32), .enable("false")) multiplexer_15 (
    .in0(register_25_q), .in1(register_26_q), .in2(register_27_q), .in3(register_28_q),
    .out(multiplexer_15_out), .sel(ReadReg2[1:0]));
  Multiplexer #(.select(2), .width(32), .enable("false")) multiplexer_16 (
    .in0(register_29_q), .in1(register_30_q), .in2(register_31_q), .in3(register_32_q),
    .out(multiplexer_7_out), .sel(ReadReg2[1:0]));
  Multiplexer #(.select(2), .width(32), .enable("false")) multiplexer_17 (
    .in0(multiplexer_9_out), .in1(multiplexer_10_out), .in2(multiplexer_11_out), .in3(multiplexer_12_out),
    .out(multiplexer_17_out), .sel(ReadReg2[3:2]));
  Multiplexer #(.select(2), .width(32), .enable("false")) multiplexer_18 (
    .in0(multiplexer_1_out), .in1(multiplexer_2_out), .in2(multiplexer_3_out), .in3(multiplexer_4_out),
    .out(multiplexer_18_out), .sel(ReadReg1[3:2]));
  Multiplexer #(.select(2), .width(32), .enable("false")) multiplexer_19 (
    .in0(multiplexer_13_out), .in1(multiplexer_14_out), .in2(multiplexer_15_out), .in3(multiplexer_7_out),
    .out(multiplexer_19_out), .sel(ReadReg2[3:2]));
  Multiplexer #(.select(2), .width(32), .enable("false")) multiplexer_20 (
    .in0(multiplexer_5_out), .in1(multiplexer_6_out), .in2(multiplexer_7_out), .in3(multiplexer_8_out),
    .out(multiplexer_20_out), .sel(ReadReg1[3:2]));
  Multiplexer #(.width(32), .enable("false")) multiplexer_21 (
    .in0(multiplexer_17_out), .in1(multiplexer_19_out), .out(ReadData1), .sel(ReadReg1[4]));
  Multiplexer #(.width(32), .enable("false")) multiplexer_22 (
    .in0(multiplexer_18_out), .in1(multiplexer_20_out), .out(ReadData2), .sel(ReadReg2[4]));
endmodule
