// Logisim project mips-datapath-lab-aoc1.circ as structural Verilog: 7 circuits, main circuit mips
module alu (
  input  [3:0] ALU_Control,
  input  [31:0] in_2,
  input  [31:0] in_3,
  output [31:0] out_4,
  output Zero
);

  wire comparator_1_lt;
  wire [31:0] adder_1_out, and_1_out, multiplexer_1_out, or_1_out, subtractor_1_out, xor_1_out;

  assign and_1_out = in_2 & in_3;  // AND_Gate and_1, 32 bits wide
  assign or_1_out = in_2 | in_3;  // OR_Gate or_1, 32 bits wide
  Adder #(.width(32)) adder_1 (.a(in_2), .b(in_3), .out(adder_1_out));  // open: cin, cout
  Subtractor #(.width(32)) subtractor_1 (.a(in_2), .b(in_3), .out(subtractor_1_out));  // open: bin, bout
  Comparator #(.width(32), .mode("unsigned")) comparator_1 (.a(in_2), .b(in_3), .lt(comparator_1_lt));  // open: gt, eq
  assign xor_1_out = in_2 ^ in_3;  // XOR_Gate xor_1, 32 bits wide
  Multiplexer #(.width(32), .enable("false")) multiplexer_1 (
    .in0({32{1'b0}}), .in1(32'h1), .out(multiplexer_1_out), .sel(comparator_1_lt));
  Multiplexer #(.select(4), .width(32), .enable("false")) multiplexer_2 (
    .in0(and_1_out), .in1(or_1_out), .in2(adder_1_out), .in6(subtractor_1_out), .in7(multiplexer_1_out),
    .in12(xor_1_out), .out(out_4), .sel(ALU_Control));  // open: in3, in4, in5, in8, in9, in10, in11, in13, in14, in15
  Comparator #(.width(32), .mode("unsigned")) comparator_2 (.a(out_4), .b({32{1'b0}}), .eq(Zero));  // open: gt, lt

  // Notes on the sheet:
  //   A
  //   B
  //   Op selects the result
  //   Output
endmodule

module mips (
);

  wire alu_1_zero, and_1_out, clock_1_out, control_1_alusrc, control_1_branch, control_1_jump,
       control_1_memread, control_1_memtoreg, control_1_memwrite, control_1_regdst, control_1_regwrite,
       Restart_Program_1d76d92f_out, Zero_Reg_File_ccad97c5_out;
  wire [1:0] control_1_aluop;
  wire [3:0] alu_control_65f38bbc_1_operation;
  wire [4:0] multiplexer_1_out;
  wire [7:0] alu_1_out_4_2;
  wire [27:0] bit_extender_1_out, shifter_1_out;
  wire [31:0] adder_1_out, adder_2_out, alu_1_out_4, bit_extender_2_out, multiplexer_2_out,
       multiplexer_3_out, multiplexer_4_out, multiplexer_5_out, PC_q, ram_1_data,
       reg_32_a222b9a7_1_readdata1, reg_32_a222b9a7_1_readdata2, rom_1_data, shifter_2_out;

  Register #(.width(32)) PC (
    .D(multiplexer_4_out), .Q(PC_q), .clk(clock_1_out), .clr(Restart_Program_1d76d92f_out));  // open: en
  Clock clock_1 (.out(clock_1_out));
  Button Restart_Program_1d76d92f (.out(Restart_Program_1d76d92f_out));
  Button Zero_Reg_File_ccad97c5 (.out(Zero_Reg_File_ccad97c5_out));
  Adder #(.width(32)) adder_1 (.a(PC_q), .b(32'h4), .out(adder_1_out));  // open: cin, cout
  // Probe on rom_1_data
  ROM #(.dataWidth(32)) rom_1 (.addr(PC_q[9:2]), .data(rom_1_data));
  assign bit_extender_1_out = {{2{rom_1_data[25]}}, rom_1_data[25:0]};  // Bit_Extender bit_extender_1
  Shifter #(.width(28)) shifter_1 (.in(bit_extender_1_out), .\dist (5'b00010), .out(shifter_1_out));
  control control_1 (
    .in_1(rom_1_data[31:26]), .RegDst(control_1_regdst), .MemRead(control_1_memread),
    .ALUOp(control_1_aluop), .MemWrite(control_1_memwrite), .MemtoReg(control_1_memtoreg),
    .ALUSrc(control_1_alusrc), .Branch(control_1_branch), .RegWrite(control_1_regwrite), .jump(control_1_jump));
  Multiplexer #(.width(5), .enable("false")) multiplexer_1 (
    .in0(rom_1_data[20:16]), .in1(rom_1_data[15:11]), .out(multiplexer_1_out), .sel(control_1_regdst));
  // Probe on multiplexer_5_out
  reg_32_a222b9a7 reg_32_a222b9a7_1 (
    .ReadReg1(rom_1_data[25:21]), .ReadReg2(rom_1_data[20:16]), .WriteReg(multiplexer_1_out),
    .RegWrite(control_1_regwrite), .ReadData1(reg_32_a222b9a7_1_readdata1),
    .ReadData2(reg_32_a222b9a7_1_readdata2), .WriteData(multiplexer_5_out), .Clk(clock_1_out),
    .Reset(Zero_Reg_File_ccad97c5_out));
  // Probe on rom_1_data[25:21]
  // Probe on rom_1_data[20:16]
  // Probe on multiplexer_1_out
  assign bit_extender_2_out = {{16{rom_1_data[15]}}, rom_1_data[15:0]};  // Bit_Extender bit_extender_2
  Shifter #(.width(32)) shifter_2 (.in(bit_extender_2_out), .\dist (5'b00010), .out(shifter_2_out));
  Multiplexer #(.width(32), .enable("false")) multiplexer_2 (
    .in0(reg_32_a222b9a7_1_readdata2), .in1(bit_extender_2_out), .out(multiplexer_2_out),
    .sel(control_1_alusrc));
  // Probe on bit_extender_2_out
  alu_control_65f38bbc alu_control_65f38bbc_1 (
    .Operation(alu_control_65f38bbc_1_operation), .ALUOp(control_1_aluop), .Function(rom_1_data[5:0]));
  alu alu_1 (
    .out_4({alu_1_out_4[31:10], alu_1_out_4_2, alu_1_out_4[1:0]}), .Zero(alu_1_zero),
    .in_2(reg_32_a222b9a7_1_readdata1), .in_3(multiplexer_2_out),
    .ALU_Control(alu_control_65f38bbc_1_operation));
  // Probe on reg_32_a222b9a7_1_readdata1
  // Probe on multiplexer_2_out
  Adder #(.width(32)) adder_2 (.a(adder_1_out), .b(shifter_2_out), .out(adder_2_out));  // open: cin, cout
  // Probe on alu_control_65f38bbc_1_operation
  Multiplexer #(.width(32), .enable("false")) multiplexer_3 (
    .in0(adder_1_out), .in1(adder_2_out), .out(multiplexer_3_out), .sel(and_1_out));
  and and_1 (and_1_out, control_1_branch, alu_1_zero);
  // Probe on multiplexer_4_out
  Multiplexer #(.width(32), .enable("false")) multiplexer_4 (
    .in0(multiplexer_3_out), .in1({adder_1_out[31:28], shifter_1_out}), .out(multiplexer_4_out),
    .sel(control_1_jump));
  // Probe on alu_1_out_4_2
  RAM #(.dataWidth(32)) ram_1 (
    .addr(alu_1_out_4_2), .data(ram_1_data), .clk(clock_1_out), .ld(control_1_memread));  // open: sel, clr
  Multiplexer #(.width(32), .enable("false")) multiplexer_5 (
    .in0({alu_1_out_4[31:10], alu_1_out_4_2, alu_1_out_4[1:0]}), .in1(ram_1_data), .out(multiplexer_5_out),
    .sel(control_1_memtoreg));

  // Notes on the sheet:
  //   Clock
  //   Current Instruction
  //   contents of rom_1 (hex, n*v repeats v):
  //   8c080000 8c090004 11090002 1095022 8100006 1095020 214a000a ac0a0008
  //   Reg Write Data
  //   Imm. Value
  //   ALU Op
  //   Next PC
  //   Mem Addr
  //   Right-click and load the 1234.mem into the RAM.
endmodule

module instruction_type_decode_f0ff2599 (
  input  [5:0] opcode,
  output R_format_48db13f9,
  output lw,
  output sw,
  output beq,
  output addi,
  output jump
);

  Comparator #(.width(6), .mode("unsigned")) comparator_1 (
    .a({6{1'b0}}), .b(opcode), .eq(R_format_48db13f9));  // open: gt, lt
  Comparator #(.width(6), .mode("unsigned")) comparator_2 (.a(6'b100011), .b(opcode), .eq(lw));  // open: gt, lt
  Comparator #(.width(6), .mode("unsigned")) comparator_3 (.a(6'b101011), .b(opcode), .eq(sw));  // open: gt, lt
  Comparator #(.width(6), .mode("unsigned")) comparator_4 (.a(6'b000100), .b(opcode), .eq(beq));  // open: gt, lt
  Comparator #(.width(6), .mode("unsigned")) comparator_5 (.a(6'b001000), .b(opcode), .eq(addi));  // open: gt, lt
  Comparator #(.width(6), .mode("unsigned")) comparator_6 (.a(6'b000010), .b(opcode), .eq(jump));  // open: gt, lt
endmodule

module control_decode_fa4be995 (
  input  Rformat,
  input  lw,
  input  sw,
  input  beq,
  input  addi,
  input  jump,
  output RegDst,
  output ALUSrc,
  output MemtoReg,
  output RegWrite,
  output MemRead,
  output MemWrite,
  output Branch,
  output ALUOp1,
  output ALUOp0,
  output jump_2
);

  wire and_1_out, and_2_out, and_3_out, and_4_out, and_5_out, and_6_out, and_7_out, and_9_out, and_10_out,
       and_11_out, not_1_out, not_2_out, not_3_out, not_4_out, not_5_out, not_6_out, not_7_out, not_8_out,
       not_9_out, not_10_out, not_11_out, not_12_out, not_13_out, not_14_out, not_15_out;

  not not_1 (not_1_out, lw);
  not not_2 (not_2_out, addi);
  not not_3 (not_3_out, lw);
  not not_4 (not_4_out, lw);
  not not_5 (not_5_out, lw);
  not not_6 (not_6_out, Rformat);
  not not_7 (not_7_out, beq);
  not not_8 (not_8_out, Rformat);
  not not_9 (not_9_out, Rformat);
  not not_10 (not_10_out, Rformat);
  not not_11 (not_11_out, sw);
  not not_12 (not_12_out, beq);
  not not_13 (not_13_out, Rformat);
  not not_14 (not_14_out, Rformat);
  not not_15 (not_15_out, Rformat);
  and and_1 (and_1_out, not_1_out, not_2_out);
  and and_2 (and_2_out, not_3_out, beq);
  and and_3 (and_3_out, not_4_out, sw);
  and and_4 (and_4_out, Rformat, not_5_out);
  and and_5 (and_5_out, not_6_out, not_7_out, addi);
  and and_6 (and_6_out, not_8_out, sw);
  and and_7 (and_7_out, not_9_out, lw);
  and and_8 (MemtoReg, not_10_out, lw);
  and and_9 (and_9_out, not_11_out, not_12_out, addi);
  and and_10 (and_10_out, not_13_out, lw);
  and and_11 (and_11_out, lw, sw, beq);
  and and_12 (MemWrite, not_14_out, sw);
  and and_13 (Branch, not_15_out, beq);
  or or_1 (RegDst, and_1_out, and_2_out, and_3_out, and_4_out);
  or or_2 (ALUSrc, and_5_out, and_6_out, and_7_out);
  or or_3 (RegWrite, and_9_out, lw, Rformat);
  or or_4 (MemRead, and_10_out, and_11_out);

  assign ALUOp0 = beq;
  assign ALUOp1 = Rformat;
  assign jump_2 = jump;
endmodule

module alu_control_65f38bbc (
  input  [5:0] Function,
  input  [1:0] ALUOp,
  output [3:0] Operation
);

  wire A_2_out, A_3_out, A_out, and_1_out, and_2_out, and_3_out, C_out, not_1_out, not_2_out, not_3_out,
       not_4_out, not_5_out, not_6_out, not_7_out, not_8_out, not_11_out, not_12_out, not_13_out, not_14_out,
       not_15_out, not_16_out, not_17_out, not_18_out, not_20_out, or_1_out, or_2_out;
  wire [2:0] priority_encoder_1_out;

  not not_1 (not_1_out, ALUOp[1]);
  not not_2 (not_2_out, ALUOp[0]);
  not not_3 (not_3_out, ALUOp[0]);
  not not_4 (not_4_out, Function[3]);
  not not_5 (not_5_out, Function[2]);
  not not_6 (not_6_out, Function[1]);
  not not_7 (not_7_out, Function[0]);
  not not_8 (not_8_out, ALUOp[1]);
  // NOT_Gate not_9 has open pins: in=Function[3], out=open
  // NOT_Gate not_10 has open pins: in=Function[2], out=open
  not not_11 (not_11_out, Function[0]);
  and and_1 (and_1_out, not_1_out, not_2_out);
  and and_2 (and_2_out, ALUOp[1], not_3_out, not_4_out, not_5_out, not_6_out, not_7_out);
  and and_3 (and_3_out, not_8_out, ALUOp[0]);
  and C (C_out, ALUOp[1], not_11_out);
  not not_12 (not_12_out, ALUOp[0]);
  not not_13 (not_13_out, Function[3]);
  and A (A_out, ALUOp[1], not_12_out, not_13_out, Function[2], not_14_out, not_15_out);
  not not_14 (not_14_out, Function[1]);
  not not_15 (not_15_out, Function[0]);
  not not_16 (not_16_out, ALUOp[0]);
  not not_17 (not_17_out, Function[3]);
  and A_2 (A_2_out, ALUOp[1], not_16_out, not_17_out, Function[2], not_18_out, Function[0]);
  not not_18 (not_18_out, Function[1]);
  and A_3 (A_3_out, ALUOp[1], not_20_out);
  // NOT_Gate not_19 has open pins: in=Function[2], out=open
  not not_20 (not_20_out, Function[0]);
  or or_1 (or_1_out, and_1_out, and_2_out);
  or or_2 (or_2_out, and_3_out, C_out);
  Priority_Encoder priority_encoder_1 (
    .in0(A_out), .in1(A_2_out), .in2(or_1_out), .in3(or_2_out), .in4(A_3_out), .out(priority_encoder_1_out));  // open: in5, in6, in7, en_in, gs, en_out
  Multiplexer #(.select(3), .width(4)) multiplexer_1 (
    .in0(4'b0000), .in1(4'b0001), .in2(4'b0010), .in3(4'b0110), .in4(4'b0111), .out(Operation),
    .sel(priority_encoder_1_out));  // open: in5, in6, in7, en

  // Notes on the sheet:
  //   Inputs
  //   B -- OR
  //   Hint: Here is the logic for the first row: 
  //   A -- if (ALUOp1=0 and ALUOp0=0)
  //   D -- then output = 2 = 0010
  //   A
  //   C
  //   B -- OR
  //   A
  //   A -- if (ALUOP1=1 and ALUOP0=0 and F3, F1 are 0 and F2, F0 are 1) 
  //   A -- if (ALUOp1=1 and F3, F1 are 1 and F2, F0 are 0)
  //   C -- if (ALUOp1=1 and ALUOp0=0 and F3, F2, F1, F0 are all 0)
  //   B
  //   A -- if (ALUOp1=0 and ALUOp0=1)
  //   C -- if (ALUOp1=1 and F1=1 and F3, F2, F0 are all 0)
  //   B
  //   A -- if (ALUOP1=1 and ALUOP0=0 and F2=1 and F3, F1, F0 are all 0) 
  //   True for 0010=2
  //   True for 0110=6
  //   True for 0000=0
  //   True for 0001=1
  //   True for 0111=7
  //   We have 5 possible outputs
  //   D
  //   Depending on which input is 1,
  //   one of the outputs above will be selected.
endmodule

module control (
  input  [5:0] in_1,
  output RegDst,
  output Branch,
  output MemRead,
  output MemtoReg,
  output [1:0] ALUOp,
  output MemWrite,
  output ALUSrc,
  output RegWrite,
  output jump
);

  wire instruction_type_decode_f0ff2599_1_addi, instruction_type_decode_f0ff2599_1_beq,
       instruction_type_decode_f0ff2599_1_jump, instruction_type_decode_f0ff2599_1_lw,
       instruction_type_decode_f0ff2599_1_r_format_48db13f9, instruction_type_decode_f0ff2599_1_sw;

  instruction_type_decode_f0ff2599 instruction_type_decode_f0ff2599_1 (
    .opcode(in_1), .R_format_48db13f9(instruction_type_decode_f0ff2599_1_r_format_48db13f9),
    .lw(instruction_type_decode_f0ff2599_1_lw), .sw(instruction_type_decode_f0ff2599_1_sw),
    .beq(instruction_type_decode_f0ff2599_1_beq), .addi(instruction_type_decode_f0ff2599_1_addi),
    .jump(instruction_type_decode_f0ff2599_1_jump));
  control_decode_fa4be995 control_decode_fa4be995_1 (
    .Rformat(instruction_type_decode_f0ff2599_1_r_format_48db13f9),
    .lw(instruction_type_decode_f0ff2599_1_lw), .RegDst(RegDst), .sw(instruction_type_decode_f0ff2599_1_sw),
    .beq(instruction_type_decode_f0ff2599_1_beq), .addi(instruction_type_decode_f0ff2599_1_addi),
    .ALUSrc(ALUSrc), .MemtoReg(MemtoReg), .RegWrite(RegWrite), .MemRead(MemRead), .MemWrite(MemWrite),
    .Branch(Branch), .ALUOp1(ALUOp[1]), .ALUOp0(ALUOp[0]), .jump(instruction_type_decode_f0ff2599_1_jump),
    .jump_2(jump));

  // Notes on the sheet:
  //   Instruction OpCode
  //   Decode the Instruction Type first
  //   From the Insturction Type,
  //   decode the control signals
endmodule

module reg_32_a222b9a7 (
  input  [4:0] ReadReg1,
  input  [4:0] ReadReg2,
  input  [4:0] WriteReg,
  input  RegWrite,
  input  [31:0] WriteData,
  input  Clk,
  input  Reset,
  output [31:0] ReadData1,
  output [31:0] ReadData2
);

  wire decoder_1_out0, decoder_1_out1, decoder_2_out0, decoder_2_out1, decoder_2_out2, decoder_2_out3,
       decoder_3_out0, decoder_3_out1, decoder_3_out2, decoder_3_out3, decoder_4_out0, decoder_4_out1,
       decoder_4_out2, decoder_4_out3, decoder_5_out0, decoder_5_out1, decoder_5_out2, decoder_5_out3,
       decoder_6_out0, decoder_6_out1, decoder_6_out2, decoder_6_out3, decoder_7_out0, decoder_7_out1,
       decoder_7_out2, decoder_7_out3, decoder_8_out0, decoder_8_out1, decoder_8_out2, decoder_8_out3,
       decoder_9_out0, decoder_9_out1, decoder_9_out2, decoder_9_out3, decoder_10_out0, decoder_10_out1,
       decoder_10_out2, decoder_10_out3, decoder_11_out0, decoder_11_out1, decoder_11_out2, decoder_11_out3;
  wire [31:0] multiplexer_1_out, multiplexer_2_out, multiplexer_3_out, multiplexer_4_out, multiplexer_5_out,
       multiplexer_6_out, multiplexer_7_out, multiplexer_8_out, multiplexer_9_out, multiplexer_10_out,
       multiplexer_13_out, multiplexer_14_out, multiplexer_15_out, multiplexer_16_out, multiplexer_17_out,
       multiplexer_18_out, multiplexer_19_out, multiplexer_20_out, multiplexer_21_out, multiplexer_22_out,
       register_1_p5, register_2_p3, register_3_p3, register_4_p3, register_5_p3, register_6_p3,
       register_7_p3, register_8_p3, register_9_p3, register_10_p3, register_11_p3, register_12_p3,
       register_13_p3, register_14_p3, register_15_p3, register_16_q, register_17_p3, register_18_p3,
       register_19_p3, register_20_p3, register_21_p3, register_22_p3, register_23_p3, register_24_p3,
       register_25_p3, register_26_p3, register_27_p3, register_28_p3, register_29_p3, register_30_p3,
       register_31_p3;

  // Probe on WriteReg
  Decoder decoder_1 (.out0(decoder_1_out0), .out1(decoder_1_out1), .sel(WriteReg[4]), .en(RegWrite));
  Decoder #(.select(2)) decoder_2 (
    .out0(decoder_2_out0), .out1(decoder_2_out1), .out2(decoder_2_out2), .out3(decoder_2_out3),
    .sel(WriteReg[3:2]), .en(decoder_1_out0));
  Decoder #(.select(2)) decoder_3 (
    .out0(decoder_3_out0), .out1(decoder_3_out1), .out2(decoder_3_out2), .out3(decoder_3_out3),
    .sel(WriteReg[1:0]), .en(decoder_2_out0));
  Decoder #(.select(2)) decoder_4 (
    .out0(decoder_4_out0), .out1(decoder_4_out1), .out2(decoder_4_out2), .out3(decoder_4_out3),
    .sel(WriteReg[1:0]), .en(decoder_2_out1));
  Decoder #(.select(2)) decoder_5 (
    .out0(decoder_5_out0), .out1(decoder_5_out1), .out2(decoder_5_out2), .out3(decoder_5_out3),
    .sel(WriteReg[1:0]), .en(decoder_2_out2));
  Decoder #(.select(2)) decoder_6 (
    .out0(decoder_6_out0), .out1(decoder_6_out1), .out2(decoder_6_out2), .out3(decoder_6_out3),
    .sel(WriteReg[1:0]), .en(decoder_2_out3));
  // Register #(.width(32)) register_1: pin names not known; wires that end beside it: WriteData, decoder_3_out1, decoder_3_out0, Reset, register_1_p5
  // Register #(.width(32)) register_2: pin names not known; wires that end beside it: WriteData, decoder_3_out2, register_2_p3
  // Register #(.width(32)) register_3: pin names not known; wires that end beside it: WriteData, decoder_3_out3, register_3_p3
  // Register #(.width(32)) register_4: pin names not known; wires that end beside it: WriteData, decoder_4_out0, register_4_p3
  // Register #(.width(32)) register_5: pin names not known; wires that end beside it: WriteData, decoder_4_out1, register_5_p3
  // Register #(.width(32)) register_6: pin names not known; wires that end beside it: WriteData, decoder_4_out2, register_6_p3
  // Register #(.width(32)) register_7: pin names not known; wires that end beside it: WriteData, decoder_4_out3, register_7_p3
  // Register #(.width(32)) register_8: pin names not known; wires that end beside it: WriteData, decoder_5_out0, register_8_p3
  // Register #(.width(32)) register_9: pin names not known; wires that end beside it: WriteData, decoder_5_out1, register_9_p3
  // Register #(.width(32)) register_10: pin names not known; wires that end beside it: WriteData, decoder_5_out2, register_10_p3
  // Register #(.width(32)) register_11: pin names not known; wires that end beside it: WriteData, decoder_5_out3, register_11_p3
  // Register #(.width(32)) register_12: pin names not known; wires that end beside it: WriteData, decoder_6_out0, register_12_p3
  // Register #(.width(32)) register_13: pin names not known; wires that end beside it: WriteData, decoder_6_out1, register_13_p3
  // Register #(.width(32)) register_14: pin names not known; wires that end beside it: WriteData, decoder_6_out2, register_14_p3
  // Register #(.width(32)) register_15: pin names not known; wires that end beside it: WriteData, decoder_6_out3, register_15_p3
  // Probe on {32{1'b0}}
  // Probe on register_1_p5
  // Probe on register_2_p3
  // Probe on register_3_p3
  // Probe on register_4_p3
  // Probe on register_5_p3
  // Probe on register_6_p3
  // Probe on register_7_p3
  // Probe on register_8_p3
  // Probe on register_9_p3
  // Probe on register_10_p3
  // Probe on register_11_p3
  // Probe on register_12_p3
  // Probe on register_13_p3
  // Probe on register_14_p3
  // Probe on register_15_p3
  // Probe on ReadReg1
  Multiplexer #(.select(2), .width(32), .enable("false")) multiplexer_1 (
    .in0({32{1'b0}}), .in1(register_1_p5), .in2(register_2_p3), .in3(register_3_p3), .out(multiplexer_1_out),
    .sel(ReadReg1[1:0]));
  Multiplexer #(.select(2), .width(32), .enable("false")) multiplexer_2 (
    .in0(register_4_p3), .in1(register_5_p3), .in2(register_6_p3), .in3(register_7_p3),
    .out(multiplexer_2_out), .sel(ReadReg1[1:0]));
  Multiplexer #(.select(2), .width(32), .enable("false")) multiplexer_3 (
    .in0(register_8_p3), .in1(register_9_p3), .in2(register_10_p3), .in3(register_11_p3),
    .out(multiplexer_3_out), .sel(ReadReg1[1:0]));
  Multiplexer #(.select(2), .width(32), .enable("false")) multiplexer_4 (
    .in0(register_12_p3), .in1(register_13_p3), .in2(register_14_p3), .in3(register_15_p3),
    .out(multiplexer_4_out), .sel(ReadReg1[1:0]));
  // Probe on ReadReg2
  Multiplexer #(.select(2), .width(32), .enable("false")) multiplexer_5 (
    .in0({32{1'b0}}), .in1(register_1_p5), .in2(register_2_p3), .in3(register_3_p3), .out(multiplexer_5_out),
    .sel(ReadReg2[1:0]));
  Multiplexer #(.select(2), .width(32), .enable("false")) multiplexer_6 (
    .in0(register_4_p3), .in1(register_5_p3), .in2(register_6_p3), .in3(register_7_p3),
    .out(multiplexer_6_out), .sel(ReadReg2[1:0]));
  Multiplexer #(.select(2), .width(32), .enable("false")) multiplexer_7 (
    .in0(register_8_p3), .in1(register_9_p3), .in2(register_10_p3), .in3(register_11_p3),
    .out(multiplexer_7_out), .sel(ReadReg2[1:0]));
  Multiplexer #(.select(2), .width(32), .enable("false")) multiplexer_8 (
    .in0(register_12_p3), .in1(register_13_p3), .in2(register_14_p3), .in3(register_15_p3),
    .out(multiplexer_8_out), .sel(ReadReg2[1:0]));
  Multiplexer #(.select(2), .width(32), .enable("false")) multiplexer_9 (
    .in0(multiplexer_5_out), .in1(multiplexer_6_out), .in2(multiplexer_7_out), .in3(multiplexer_8_out),
    .out(multiplexer_9_out), .sel(ReadReg2[3:2]));
  Multiplexer #(.select(2), .width(32), .enable("false")) multiplexer_10 (
    .in0(multiplexer_1_out), .in1(multiplexer_2_out), .in2(multiplexer_3_out), .in3(multiplexer_4_out),
    .out(multiplexer_10_out), .sel(ReadReg1[3:2]));
  Decoder #(.select(2)) decoder_7 (
    .out0(decoder_7_out0), .out1(decoder_7_out1), .out2(decoder_7_out2), .out3(decoder_7_out3),
    .sel(WriteReg[3:2]), .en(decoder_1_out1));
  Decoder #(.select(2)) decoder_8 (
    .out0(decoder_8_out0), .out1(decoder_8_out1), .out2(decoder_8_out2), .out3(decoder_8_out3),
    .sel(WriteReg[1:0]), .en(decoder_7_out0));
  Decoder #(.select(2)) decoder_9 (
    .out0(decoder_9_out0), .out1(decoder_9_out1), .out2(decoder_9_out2), .out3(decoder_9_out3),
    .sel(WriteReg[1:0]), .en(decoder_7_out1));
  Decoder #(.select(2)) decoder_10 (
    .out0(decoder_10_out0), .out1(decoder_10_out1), .out2(decoder_10_out2), .out3(decoder_10_out3),
    .sel(WriteReg[1:0]), .en(decoder_7_out2));
  Decoder #(.select(2)) decoder_11 (
    .out0(decoder_11_out0), .out1(decoder_11_out1), .out2(decoder_11_out2), .out3(decoder_11_out3),
    .sel(WriteReg[1:0]), .en(decoder_7_out3));
  Register #(.width(32)) register_16 (.D(WriteData), .en(decoder_8_out0), .Q(register_16_q), .clk(Clk), .clr(Reset));
  // Register #(.width(32)) register_17: pin names not known; wires that end beside it: WriteData, decoder_8_out1, register_17_p3
  // Register #(.width(32)) register_18: pin names not known; wires that end beside it: WriteData, decoder_8_out2, register_18_p3
  // Register #(.width(32)) register_19: pin names not known; wires that end beside it: WriteData, decoder_8_out3, register_19_p3
  // Register #(.width(32)) register_20: pin names not known; wires that end beside it: WriteData, decoder_9_out0, register_20_p3
  // Register #(.width(32)) register_21: pin names not known; wires that end beside it: WriteData, decoder_9_out1, register_21_p3
  // Register #(.width(32)) register_22: pin names not known; wires that end beside it: WriteData, decoder_9_out2, register_22_p3
  // Register #(.width(32)) register_23: pin names not known; wires that end beside it: WriteData, decoder_9_out3, register_23_p3
  // Register #(.width(32)) register_24: pin names not known; wires that end beside it: WriteData, decoder_10_out0, register_24_p3
  // Register #(.width(32)) register_25: pin names not known; wires that end beside it: WriteData, decoder_10_out1, register_25_p3
  // Register #(.width(32)) register_26: pin names not known; wires that end beside it: WriteData, decoder_10_out2, register_26_p3
  // Register #(.width(32)) register_27: pin names not known; wires that end beside it: WriteData, decoder_10_out3, register_27_p3
  // Register #(.width(32)) register_28: pin names not known; wires that end beside it: WriteData, decoder_11_out0, register_28_p3
  // Register #(.width(32)) register_29: pin names not known; wires that end beside it: WriteData, decoder_11_out1, register_29_p3
  // Register #(.width(32)) register_30: pin names not known; wires that end beside it: WriteData, decoder_11_out2, register_30_p3
  // Register #(.width(32)) register_31: pin names not known; wires that end beside it: WriteData, decoder_11_out3, register_31_p3
  // Probe on register_16_q
  // Probe on register_17_p3
  // Probe on register_18_p3
  // Probe on register_19_p3
  // Probe on register_20_p3
  // Probe on register_21_p3
  // Probe on register_22_p3
  // Probe on register_23_p3
  // Probe on register_24_p3
  // Probe on register_25_p3
  // Probe on register_26_p3
  // Probe on register_27_p3
  // Probe on register_28_p3
  // Probe on register_29_p3
  // Probe on register_30_p3
  // Probe on register_31_p3
  Multiplexer #(.width(32), .enable("false")) multiplexer_11 (
    .in0(multiplexer_10_out), .in1(multiplexer_21_out), .out(ReadData1), .sel(ReadReg1[4]));
  Multiplexer #(.width(32), .enable("false")) multiplexer_12 (
    .in0(multiplexer_9_out), .in1(multiplexer_22_out), .out(ReadData2), .sel(ReadReg2[4]));
  Multiplexer #(.select(2), .width(32), .enable("false")) multiplexer_13 (
    .in0(register_16_q), .in1(register_17_p3), .in2(register_18_p3), .in3(register_19_p3),
    .out(multiplexer_13_out), .sel(ReadReg1[1:0]));
  Multiplexer #(.select(2), .width(32), .enable("false")) multiplexer_14 (
    .in0(register_20_p3), .in1(register_21_p3), .in2(register_22_p3), .in3(register_23_p3),
    .out(multiplexer_14_out), .sel(ReadReg1[1:0]));
  Multiplexer #(.select(2), .width(32), .enable("false")) multiplexer_15 (
    .in0(register_24_p3), .in1(register_25_p3), .in2(register_26_p3), .in3(register_27_p3),
    .out(multiplexer_15_out), .sel(ReadReg1[1:0]));
  Multiplexer #(.select(2), .width(32), .enable("false")) multiplexer_16 (
    .in0(register_28_p3), .in1(register_29_p3), .in2(register_30_p3), .in3(register_31_p3),
    .out(multiplexer_16_out), .sel(ReadReg1[1:0]));
  Multiplexer #(.select(2), .width(32), .enable("false")) multiplexer_17 (
    .in0(register_16_q), .in1(register_17_p3), .in2(register_18_p3), .in3(register_19_p3),
    .out(multiplexer_17_out), .sel(ReadReg2[1:0]));
  Multiplexer #(.select(2), .width(32), .enable("false")) multiplexer_18 (
    .in0(register_20_p3), .in1(register_21_p3), .in2(register_22_p3), .in3(register_23_p3),
    .out(multiplexer_18_out), .sel(ReadReg2[1:0]));
  Multiplexer #(.select(2), .width(32), .enable("false")) multiplexer_19 (
    .in0(register_24_p3), .in1(register_25_p3), .in2(register_26_p3), .in3(register_27_p3),
    .out(multiplexer_19_out), .sel(ReadReg2[1:0]));
  Multiplexer #(.select(2), .width(32), .enable("false")) multiplexer_20 (
    .in0(register_28_p3), .in1(register_29_p3), .in2(register_30_p3), .in3(register_31_p3),
    .out(multiplexer_20_out), .sel(ReadReg2[1:0]));
  Multiplexer #(.select(2), .width(32), .enable("false")) multiplexer_21 (
    .in0(multiplexer_17_out), .in1(multiplexer_18_out), .in2(multiplexer_19_out), .in3(multiplexer_20_out),
    .out(multiplexer_21_out), .sel(ReadReg2[3:2]));
  Multiplexer #(.select(2), .width(32), .enable("false")) multiplexer_22 (
    .in0(multiplexer_13_out), .in1(multiplexer_14_out), .in2(multiplexer_15_out), .in3(multiplexer_16_out),
    .out(multiplexer_22_out), .sel(ReadReg1[3:2]));
endmodule
